// Logisim project decoding.circ as structural Verilog: 2 circuits, main circuit main
module main (
  input  [31:0] a,
  input  [31:0] b,
  input  [4:0] shamt,
  input  [3:0] operation,
  output [31:0] result,
  output zero,
  output overflow
);

  wire [31:0] and_1_out, multiplexer_1_out, or_1_out, shifter_1_out;

  assign and_1_out = a & b;  // AND_Gate and_1, 32 bits wide
  assign or_1_out = a | b;  // OR_Gate or_1, 32 bits wide
  Shifter #(.width(32)) shifter_1 (.in(b), .\dist (shamt), .out(shifter_1_out));
  Multiplexer #(.select(4), .width(32), .enable("false")) multiplexer_1 (
    .in0(and_1_out), .in1(or_1_out), .in2(shifter_1_out), .out(multiplexer_1_out), .sel(operation));  // open: in3, in4, in5, in6, in7, in8, in9, in10, in11, in12, in13, in14, in15
endmodule

module banco (
  input  [4:0] in_1,
  input  [4:0] in_2,
  input  [4:0] in_3,
  input  [31:0] in_4
);
endmodule
