// Logisim project banco_registradoderes.circ as structural Verilog: 6 circuits, main circuit main
module main (
  input  in_1,
  input  [31:0] Entradas_D,
  output [31:0] Saidas_Q
);

  D_Flip_Flop _00 (.clk(in_1), .D(Entradas_D[0]), .Q(Saidas_Q[0]));  // open: Qn, preset, en, reset
  D_Flip_Flop _01 (.clk(in_1), .D(Entradas_D[1]), .Q(Saidas_Q[1]));  // open: Qn, preset, en, reset
  D_Flip_Flop _02 (.clk(in_1), .D(Entradas_D[2]), .Q(Saidas_Q[2]));  // open: Qn, preset, en, reset
  D_Flip_Flop _03 (.clk(in_1), .D(Entradas_D[3]), .Q(Saidas_Q[3]));  // open: Qn, preset, en, reset
  D_Flip_Flop _04 (.clk(in_1), .D(Entradas_D[4]), .Q(Saidas_Q[4]));  // open: Qn, preset, en, reset
  D_Flip_Flop _05 (.clk(in_1), .D(Entradas_D[5]), .Q(Saidas_Q[5]));  // open: Qn, preset, en, reset
  D_Flip_Flop _06 (.clk(in_1), .D(Entradas_D[6]), .Q(Saidas_Q[6]));  // open: Qn, preset, en, reset
  D_Flip_Flop _07 (.clk(in_1), .D(Entradas_D[7]), .Q(Saidas_Q[7]));  // open: Qn, preset, en, reset
  D_Flip_Flop _08 (.clk(in_1), .D(Entradas_D[8]), .Q(Saidas_Q[8]));  // open: Qn, preset, en, reset
  D_Flip_Flop _09 (.clk(in_1), .D(Entradas_D[9]), .Q(Saidas_Q[9]));  // open: Qn, preset, en, reset
  D_Flip_Flop _10 (.clk(in_1), .D(Entradas_D[10]), .Q(Saidas_Q[10]));  // open: Qn, preset, en, reset
  D_Flip_Flop _11 (.clk(in_1), .D(Entradas_D[11]), .Q(Saidas_Q[11]));  // open: Qn, preset, en, reset
  D_Flip_Flop _12 (.clk(in_1), .D(Entradas_D[12]), .Q(Saidas_Q[12]));  // open: Qn, preset, en, reset
  D_Flip_Flop _13 (.clk(in_1), .D(Entradas_D[13]), .Q(Saidas_Q[13]));  // open: Qn, preset, en, reset
  D_Flip_Flop _14 (.clk(in_1), .D(Entradas_D[14]), .Q(Saidas_Q[14]));  // open: Qn, preset, en, reset
  D_Flip_Flop _15 (.clk(in_1), .D(Entradas_D[15]), .Q(Saidas_Q[15]));  // open: Qn, preset, en, reset
  D_Flip_Flop _16 (.clk(in_1), .D(Entradas_D[16]), .Q(Saidas_Q[16]));  // open: Qn, preset, en, reset
  D_Flip_Flop _17 (.clk(in_1), .D(Entradas_D[17]), .Q(Saidas_Q[17]));  // open: Qn, preset, en, reset
  D_Flip_Flop _18 (.clk(in_1), .D(Entradas_D[18]), .Q(Saidas_Q[18]));  // open: Qn, preset, en, reset
  D_Flip_Flop _19 (.clk(in_1), .D(Entradas_D[19]), .Q(Saidas_Q[19]));  // open: Qn, preset, en, reset
  D_Flip_Flop _20 (.clk(in_1), .D(Entradas_D[20]), .Q(Saidas_Q[20]));  // open: Qn, preset, en, reset
  D_Flip_Flop _21 (.clk(in_1), .D(Entradas_D[21]), .Q(Saidas_Q[21]));  // open: Qn, preset, en, reset
  D_Flip_Flop _22 (.clk(in_1), .D(Entradas_D[22]), .Q(Saidas_Q[22]));  // open: Qn, preset, en, reset
  D_Flip_Flop _23 (.clk(in_1), .D(Entradas_D[23]), .Q(Saidas_Q[23]));  // open: Qn, preset, en, reset
  D_Flip_Flop _24 (.clk(in_1), .D(Entradas_D[24]), .Q(Saidas_Q[24]));  // open: Qn, preset, en, reset
  D_Flip_Flop _25 (.clk(in_1), .D(Entradas_D[25]), .Q(Saidas_Q[25]));  // open: Qn, preset, en, reset
  D_Flip_Flop _26 (.clk(in_1), .D(Entradas_D[26]), .Q(Saidas_Q[26]));  // open: Qn, preset, en, reset
  D_Flip_Flop _27 (.clk(in_1), .D(Entradas_D[27]), .Q(Saidas_Q[27]));  // open: Qn, preset, en, reset
  D_Flip_Flop _28 (.clk(in_1), .D(Entradas_D[28]), .Q(Saidas_Q[28]));  // open: Qn, preset, en, reset
  D_Flip_Flop _29 (.clk(in_1), .D(Entradas_D[29]), .Q(Saidas_Q[29]));  // open: Qn, preset, en, reset
  D_Flip_Flop _30 (.clk(in_1), .D(Entradas_D[30]), .Q(Saidas_Q[30]));  // open: Qn, preset, en, reset
  D_Flip_Flop _31 (.clk(in_1), .D(Entradas_D[31]), .Q(Saidas_Q[31]));  // open: Qn, preset, en, reset
endmodule

// Reg
module register (
  input  en,
  input  clear,
  input  clock,
  input  [31:0] Entradas_D,
  output [31:0] Saidas_Q
);

  D_Flip_Flop _00 (.clk(clock), .D(Entradas_D[0]), .Q(Saidas_Q[0]), .en(en), .reset(clear));  // open: Qn, preset
  D_Flip_Flop _01 (.clk(clock), .D(Entradas_D[1]), .Q(Saidas_Q[1]), .reset(clear));  // open: Qn, preset, en
  D_Flip_Flop _02 (.clk(clock), .D(Entradas_D[2]), .Q(Saidas_Q[2]), .reset(clear));  // open: Qn, preset, en
  D_Flip_Flop _03 (.clk(clock), .D(Entradas_D[3]), .Q(Saidas_Q[3]), .reset(clear));  // open: Qn, preset, en
  D_Flip_Flop _04 (.clk(clock), .D(Entradas_D[4]), .Q(Saidas_Q[4]), .reset(clear));  // open: Qn, preset, en
  D_Flip_Flop _05 (.clk(clock), .D(Entradas_D[5]), .Q(Saidas_Q[5]), .reset(clear));  // open: Qn, preset, en
  D_Flip_Flop _06 (.clk(clock), .D(Entradas_D[6]), .Q(Saidas_Q[6]), .reset(clear));  // open: Qn, preset, en
  D_Flip_Flop _07 (.clk(clock), .D(Entradas_D[7]), .Q(Saidas_Q[7]), .reset(clear));  // open: Qn, preset, en
  D_Flip_Flop _08 (.clk(clock), .D(Entradas_D[8]), .Q(Saidas_Q[8]), .en(en), .reset(clear));  // open: Qn, preset
  D_Flip_Flop _09 (.clk(clock), .D(Entradas_D[9]), .Q(Saidas_Q[9]), .en(en), .reset(clear));  // open: Qn, preset
  D_Flip_Flop _10 (.clk(clock), .D(Entradas_D[10]), .Q(Saidas_Q[10]), .en(en), .reset(clear));  // open: Qn, preset
  D_Flip_Flop _11 (.clk(clock), .D(Entradas_D[11]), .Q(Saidas_Q[11]), .en(en), .reset(clear));  // open: Qn, preset
  D_Flip_Flop _12 (.clk(clock), .D(Entradas_D[12]), .Q(Saidas_Q[12]), .en(en), .reset(clear));  // open: Qn, preset
  D_Flip_Flop _13 (.clk(clock), .D(Entradas_D[13]), .Q(Saidas_Q[13]), .en(en), .reset(clear));  // open: Qn, preset
  D_Flip_Flop _14 (.clk(clock), .D(Entradas_D[14]), .Q(Saidas_Q[14]), .en(en), .reset(clear));  // open: Qn, preset
  D_Flip_Flop _15 (.clk(clock), .D(Entradas_D[15]), .Q(Saidas_Q[15]), .en(en), .reset(clear));  // open: Qn, preset
  D_Flip_Flop _16 (.clk(clock), .D(Entradas_D[16]), .Q(Saidas_Q[16]), .en(en), .reset(clear));  // open: Qn, preset
  D_Flip_Flop _17 (.clk(clock), .D(Entradas_D[17]), .Q(Saidas_Q[17]), .en(en), .reset(clear));  // open: Qn, preset
  D_Flip_Flop _18 (.clk(clock), .D(Entradas_D[18]), .Q(Saidas_Q[18]), .en(en), .reset(clear));  // open: Qn, preset
  D_Flip_Flop _19 (.clk(clock), .D(Entradas_D[19]), .Q(Saidas_Q[19]), .en(en), .reset(clear));  // open: Qn, preset
  D_Flip_Flop _20 (.clk(clock), .D(Entradas_D[20]), .Q(Saidas_Q[20]), .en(en), .reset(clear));  // open: Qn, preset
  D_Flip_Flop _21 (.clk(clock), .D(Entradas_D[21]), .Q(Saidas_Q[21]), .en(en), .reset(clear));  // open: Qn, preset
  D_Flip_Flop _22 (.clk(clock), .D(Entradas_D[22]), .Q(Saidas_Q[22]), .en(en), .reset(clear));  // open: Qn, preset
  D_Flip_Flop _23 (.clk(clock), .D(Entradas_D[23]), .Q(Saidas_Q[23]), .reset(clear));  // open: Qn, preset, en
  D_Flip_Flop _24 (.clk(clock), .D(Entradas_D[24]), .Q(Saidas_Q[24]), .en(en), .reset(clear));  // open: Qn, preset
  D_Flip_Flop _25 (.clk(clock), .D(Entradas_D[25]), .Q(Saidas_Q[25]), .en(en), .reset(clear));  // open: Qn, preset
  D_Flip_Flop _26 (.clk(clock), .D(Entradas_D[26]), .Q(Saidas_Q[26]), .en(en), .reset(clear));  // open: Qn, preset
  D_Flip_Flop _27 (.clk(clock), .D(Entradas_D[27]), .Q(Saidas_Q[27]), .en(en), .reset(clear));  // open: Qn, preset
  D_Flip_Flop _28 (.clk(clock), .D(Entradas_D[28]), .Q(Saidas_Q[28]), .en(en), .reset(clear));  // open: Qn, preset
  D_Flip_Flop _29 (.clk(clock), .D(Entradas_D[29]), .Q(Saidas_Q[29]), .en(en), .reset(clear));  // open: Qn, preset
  D_Flip_Flop _30 (.clk(clock), .D(Entradas_D[30]), .Q(Saidas_Q[30]), .reset(clear));  // open: Qn, preset, en
  D_Flip_Flop _31 (.clk(clock), .D(Entradas_D[31]), .Q(Saidas_Q[31]), .en(en), .reset(clear));  // open: Qn, preset

  // Notes on the sheet:
  //   REGISTRADOR FORMADO POR 32 FLIP-FLOPS D
  //   CIRCUITO DE UM REGISTRADOR
endmodule

// REGISTERS
module banco (
  input  [4:0] read_2,
  input  [4:0] read_1,
  input  [31:0] write_data,
  input  [4:0] write_register,
  input  clock,
  input  clear,
  input  regWrite,
  output [31:0] out_8,
  output [31:0] out_9,
  output [31:0] read_data_1,
  output [31:0] read_data_2
);

  wire we00, we01, we02, we03, we04, we05, we06, we07, we08, we09, we10, we11, we12, we13, we14, we15, we16,
       we17, we18, we19, we20, we21, we22, we23, we24, we25, we26, we27, we28, we29, we30, we31;
  wire [31:0] s00, s01, s02, s03, s04, s05, s06, s07, s08, s09, s10, s11, s12, s13, s14, s15, s16, s17, s18,
       s19, s20, s21, s22, s23, s24, s25, s26, s27, s28, s29, s30, s31, wd00, wd03, wd04, wd05, wd06, wd07,
       wd08, wd09, wd10, wd11, wd12, wd13, wd14, wd15, wd16, wd17, wd18, wd19, wd20, wd21, wd22, wd23, wd24,
       wd25, wd26, wd27, wd28, wd29, wd30, wd31;

  Demultiplexer #(.select(5)) demultiplexer_1 (
    .out0(we00), .out1(we01), .out2(we02), .out3(we03), .out4(we04), .out5(we05), .out6(we06), .out7(we07),
    .out8(we08), .out9(we09), .out10(we10), .out11(we11), .out12(we12), .out13(we13), .out14(we14),
    .out15(we15), .out16(we16), .out17(we17), .out18(we18), .out19(we19), .out20(we20), .out21(we21),
    .out22(we22), .out23(we23), .out24(we24), .out25(we25), .out26(we26), .out27(we27), .out28(we28),
    .out29(we29), .out30(we30), .out31(we31), .in(regWrite), .sel(write_register));  // open: en
  Demultiplexer #(.select(5), .width(32)) demultiplexer_2 (
    .out0(wd00), .out1(out_9), .out2(out_8), .out3(wd03), .out4(wd04), .out5(wd05), .out6(wd06), .out7(wd07),
    .out8(wd08), .out9(wd09), .out10(wd10), .out11(wd11), .out12(wd12), .out13(wd13), .out14(wd14),
    .out15(wd15), .out16(wd16), .out17(wd17), .out18(wd18), .out19(wd19), .out20(wd20), .out21(wd21),
    .out22(wd22), .out23(wd23), .out24(wd24), .out25(wd25), .out26(wd26), .out27(wd27), .out28(wd28),
    .out29(wd29), .out30(wd30), .out31(wd31), .in(write_data), .sel(write_register));  // open: en
  register zero (.en(we00), .clear(clear), .clock(clock), .Entradas_D({32{1'b0}}), .Saidas_Q(s00));
  register a0 (.en(we04), .clear(clear), .clock(clock), .Entradas_D(wd04), .Saidas_Q(s04));
  register t0 (.en(we08), .clear(clear), .clock(clock), .Entradas_D(wd08), .Saidas_Q(s08));
  register t4 (.en(we12), .clear(clear), .clock(clock), .Entradas_D(wd12), .Saidas_Q(s12));
  register s0 (.en(we16), .clear(clear), .clock(clock), .Entradas_D(wd16), .Saidas_Q(s16));
  register s4 (.en(we20), .clear(clear), .clock(clock), .Entradas_D(wd20), .Saidas_Q(s20));
  register t8 (.en(we24), .clear(clear), .clock(clock), .Entradas_D(wd24), .Saidas_Q(s24));
  register gp (.en(we28), .clear(clear), .clock(clock), .Entradas_D(wd28), .Saidas_Q(s28));
  register at (.en(we01), .clear(clear), .clock(clock), .Entradas_D(out_9), .Saidas_Q(s01));
  register a1 (.en(we05), .clear(clear), .clock(clock), .Entradas_D(wd05), .Saidas_Q(s05));
  register t1 (.en(we09), .clear(clear), .clock(clock), .Entradas_D(wd09), .Saidas_Q(s09));
  register t5 (.en(we13), .clear(clear), .clock(clock), .Entradas_D(wd13), .Saidas_Q(s13));
  register s1 (.en(we17), .clear(clear), .clock(clock), .Entradas_D(wd17), .Saidas_Q(s17));
  register s5 (.en(we21), .clear(clear), .clock(clock), .Entradas_D(wd21), .Saidas_Q(s21));
  register t9 (.en(we25), .clear(clear), .clock(clock), .Entradas_D(wd25), .Saidas_Q(s25));
  register sp (.en(we29), .clear(clear), .clock(clock), .Entradas_D(wd29), .Saidas_Q(s29));
  register v0 (.en(we02), .clear(clear), .clock(clock), .Entradas_D(out_8), .Saidas_Q(s02));
  register a2 (.en(we06), .clear(clear), .clock(clock), .Entradas_D(wd06), .Saidas_Q(s06));
  register t2 (.en(we10), .clear(clear), .clock(clock), .Entradas_D(wd10), .Saidas_Q(s10));
  register t6 (.en(we14), .clear(clear), .clock(clock), .Entradas_D(wd14), .Saidas_Q(s14));
  register s2 (.en(we18), .clear(clear), .clock(clock), .Entradas_D(wd18), .Saidas_Q(s18));
  register s6 (.en(we22), .clear(clear), .clock(clock), .Entradas_D(wd22), .Saidas_Q(s22));
  register k0 (.en(we26), .clear(clear), .clock(clock), .Entradas_D(wd26), .Saidas_Q(s26));
  register fp (.en(we30), .clear(clear), .clock(clock), .Entradas_D(wd30), .Saidas_Q(s30));
  register v1 (.en(we03), .clear(clear), .clock(clock), .Entradas_D(wd03), .Saidas_Q(s03));
  register a3 (.en(we07), .clear(clear), .clock(clock), .Entradas_D(wd07), .Saidas_Q(s07));
  register t3 (.en(we11), .clear(clear), .clock(clock), .Entradas_D(wd11), .Saidas_Q(s11));
  register t7 (.en(we15), .clear(clear), .clock(clock), .Entradas_D(wd15), .Saidas_Q(s15));
  register s3 (.en(we19), .clear(clear), .clock(clock), .Entradas_D(wd19), .Saidas_Q(s19));
  register s7 (.en(we23), .clear(clear), .clock(clock), .Entradas_D(wd23), .Saidas_Q(s23));
  register k1 (.en(we27), .clear(clear), .clock(clock), .Entradas_D(wd27), .Saidas_Q(s27));
  register ra (.en(we31), .clear(clear), .clock(clock), .Entradas_D(wd31), .Saidas_Q(s31));
  Multiplexer #(.select(5), .width(32)) multiplexer_1 (
    .in0(s00), .in1(s01), .in2(s02), .in3(s03), .in4(s04), .in5(s05), .in6(s06), .in7(s07), .in8(s08),
    .in9(s09), .in10(s10), .in11(s11), .in12(s12), .in13(s13), .in14(s14), .in15(s15), .in16(s16),
    .in17(s17), .in18(s18), .in19(s19), .in20(s20), .in21(s21), .in22(s22), .in23(s23), .in24(s24),
    .in25(s25), .in26(s26), .in27(s27), .in28(s28), .in29(s29), .in30(s30), .in31(s31), .out(read_data_1),
    .sel(read_1));  // open: en
  Multiplexer #(.select(5), .width(32)) multiplexer_2 (
    .in0(s00), .in1(s01), .in2(s02), .in3(s03), .in4(s04), .in5(s05), .in6(s06), .in7(s07), .in8(s08),
    .in9(s09), .in10(s10), .in11(s11), .in12(s12), .in13(s13), .in14(s14), .in15(s15), .in16(s16),
    .in17(s17), .in18(s18), .in19(s19), .in20(s20), .in21(s21), .in22(s22), .in23(s23), .in24(s24),
    .in25(s25), .in26(s26), .in27(s27), .in28(s28), .in29(s29), .in30(s30), .in31(s31), .out(read_data_2),
    .sel(read_2));  // open: en

  // Other names for the same wires on the sheet: wd01[31:0] = out_9; wd02[31:0] = out_8
endmodule

// ULA
module testUla (
  input  [31:0] in_1,
  input  [31:0] in_2,
  input  [3:0] in_3,
  input  [4:0] in_4,
  output ZERO,
  output [31:0] out_6,
  output Overflow
);

  wire and_1_out, and_2_out, and_3_out, comparator_1_gt, \Só_ADD_out , \Só_SUB_out , xor_1_out;
  wire [0:0] comparator_1_eq, comparator_1_lt;
  wire [31:0] _000_out, _001_out, _010_out, _011_out, adder_1_out, shifter_1_out, shifter_2_out,
       subtractor_1_out;

  assign _000_out = in_1 & in_2;  // AND_Gate _000, 32 bits wide
  assign _001_out = in_1 | in_2;  // OR_Gate _001, 32 bits wide
  assign _010_out = ~(in_1 | in_2);  // NOR_Gate _010, 32 bits wide
  assign _011_out = in_1 ^ in_2;  // XOR_Gate _011, 32 bits wide
  Comparator #(.width(32)) comparator_1 (
    .a(in_1), .b(in_2), .gt(comparator_1_gt), .eq(comparator_1_eq[0]), .lt(comparator_1_lt[0]));
  Adder #(.width(32)) adder_1 (.a(in_1), .b(in_2), .out(adder_1_out));  // open: cin, cout
  Subtractor #(.width(32)) subtractor_1 (.a(in_1), .b(in_2), .out(subtractor_1_out));  // open: bin, bout
  Shifter #(.width(32)) shifter_1 (.in(in_1), .\dist (in_4), .out(shifter_1_out));
  Shifter #(.width(32), .shift("lr")) shifter_2 (.in(in_1), .\dist (in_4), .out(shifter_2_out));
  Multiplexer #(.select(4), .width(32)) multiplexer_1 (
    .in0(_000_out), .in1(_001_out), .in2(_010_out), .in3(_011_out), .in4({{31{1'b0}}, comparator_1_eq[0]}),
    .in5({{31{1'b0}}, comparator_1_lt[0]}), .in6(adder_1_out), .in7(subtractor_1_out), .in8(shifter_1_out),
    .in9(shifter_2_out), .out(out_6), .sel(in_3));  // open: in10, in11, in12, in13, in14, in15, en
  nor nor_1 (ZERO, out_6[31], out_6[30], out_6[29], out_6[28], out_6[27], out_6[26], out_6[25], out_6[24], out_6[23], out_6[22], out_6[21], out_6[20], out_6[19], out_6[18], out_6[17], out_6[16], out_6[15], out_6[14], out_6[13], out_6[12], out_6[11], out_6[10], out_6[9], out_6[8], out_6[7], out_6[6], out_6[5], out_6[4], out_6[3], out_6[2], out_6[1], out_6[0]);
  and and_1 (and_1_out, in_2[31], in_1[31]);
  and \Só_SUB  (\Só_SUB_out , ~in_3[0], in_3[1], in_3[2], ~in_3[3]);  // AND_Gate
  xor xor_1 (xor_1_out, out_6[31], and_1_out);
  and \Só_ADD  (\Só_ADD_out , ~in_3[0], in_3[1], in_3[2], ~in_3[3]);  // AND_Gate
  and and_2 (and_2_out, out_6[31], ~in_2[31], in_1[31], \Só_SUB_out );  // AND_Gate
  and and_3 (and_3_out, xor_1_out, \Só_ADD_out );
  or or_1 (Overflow, and_2_out, and_3_out);

  // Other names for the same wires on the sheet: A[31:0] = in_1; B[31:0] = in_2; Operação_ALU[3:0] = in_3;
  //   RESULTADO[31:0] = out_6; SHAMT[4:0] = in_4

  // Notes on the sheet:
  //   CASOS OVERFLOW
  //   ADD overflow se:
  //   SUB overflow se:
  //   (+x)+ (+y) = - 
  //   	(-x)+ (-y) = +
  //   (-a) - (+b) =  + 
  //   (+a) - (-b) = - 
  //   100
  //   101
  //   110
  //   111
  //   1000
  //   1001
  //   Casos Subtração
  //   Casos Adição
  //   MSB de Resultado
  //   MSB operando B
  //   MSB operando A
endmodule

module conection (
  input  [4:0] WRITE_REGISTER,
  input  [4:0] READ_REGISTER_1,
  input  [4:0] READ_REGISTER_2,
  input  [31:0] WRITE_DATA,
  input  [3:0] OPERATION,
  input  CLEAR,
  input  REG_WRITE,
  input  [4:0] SHAMP,
  output [31:0] SAIDA_DA_ULA
);

  wire clock_1_out;
  wire [31:0] banco_1_read_data_1, banco_1_read_data_2;

  Clock clock_1 (.out(clock_1_out));
  banco banco_1 (
    .read_2(READ_REGISTER_2), .read_1(READ_REGISTER_1), .write_data(WRITE_DATA),
    .write_register(WRITE_REGISTER), .clock(clock_1_out), .clear(CLEAR), .regWrite(REG_WRITE),
    .read_data_1(banco_1_read_data_1), .read_data_2(banco_1_read_data_2));  // open: out_9, out_8
  testUla testula_1 (
    .in_1(banco_1_read_data_1), .in_2(banco_1_read_data_2), .in_3(OPERATION), .in_4(SHAMP),
    .out_6(SAIDA_DA_ULA));  // open: ZERO, Overflow
endmodule

module testUla2 (
  input  [31:0] A,
  input  [31:0] B,
  input  [3:0] OP,
  input  [4:0] SHAMT,
  output [31:0] out_5,
  output ZERO,
  output OVERFLOW
);

  wire and_2_out, and_3_out, and_4_out, and_5_out, and_6_out, and_7_out, and_8_out, and_9_out, and_10_out,
       and_11_out, and_12_out, nor_2_out, or_2_out, or_4_out;
  wire [0:0] comparator_2_eq, comparator_2_lt;
  wire [31:0] adder_1_out, and_1_out, nor_1_out, or_1_out, shifter_1_out, shifter_2_out, subtractor_1_out,
       xor_1_out;

  Comparator #(.width(32)) comparator_1 (.a({32{1'b0}}), .b(out_5), .eq(ZERO));  // open: gt, lt
  assign and_1_out = A & B;  // AND_Gate and_1, 32 bits wide
  assign or_1_out = A | B;  // OR_Gate or_1, 32 bits wide
  assign nor_1_out = ~(A | B);  // NOR_Gate nor_1, 32 bits wide
  assign xor_1_out = A ^ B;  // XOR_Gate xor_1, 32 bits wide
  Shifter #(.width(32)) shifter_1 (.in(A), .\dist (SHAMT), .out(shifter_1_out));
  Shifter #(.width(32), .shift("lr")) shifter_2 (.in(A), .\dist (SHAMT), .out(shifter_2_out));
  Adder #(.width(32)) adder_1 (.a(A), .b(B), .out(adder_1_out));  // open: cin, cout
  Subtractor #(.width(32)) subtractor_1 (.a(A), .b(B), .out(subtractor_1_out));  // open: bin, bout
  Comparator #(.width(32)) comparator_2 (.a(A), .b(B), .eq(comparator_2_eq[0]), .lt(comparator_2_lt[0]));  // open: gt
  Multiplexer #(.select(4), .width(32)) multiplexer_1 (
    .in0(and_1_out), .in1(or_1_out), .in2(nor_1_out), .in3(xor_1_out), .in4(shifter_1_out),
    .in5(shifter_2_out), .in6(adder_1_out), .in7(subtractor_1_out), .in8({{31{1'b0}}, comparator_2_eq[0]}),
    .in9({{31{1'b0}}, comparator_2_lt[0]}), .in10({32{1'b0}}), .in11({32{1'b0}}), .in12({32{1'b0}}),
    .in13({32{1'b0}}), .in14({32{1'b0}}), .in15({32{1'b0}}), .out(out_5), .sel(OP));  // open: en
  nor nor_2 (nor_2_out, A[31], B[31]);
  and and_2 (and_2_out, nor_2_out, out_5[31]);
  and and_3 (and_3_out, A[31], B[31]);
  and and_4 (and_4_out, and_3_out, ~out_5[31]);  // AND_Gate
  or or_2 (or_2_out, and_2_out, and_4_out);
  and and_5 (and_5_out, ~OP[0], OP[1], OP[2], ~OP[3]);  // AND_Gate
  and and_6 (and_6_out, and_5_out, or_2_out);
  or or_3 (OVERFLOW, and_6_out, and_9_out);
  and and_7 (and_7_out, ~A[31], B[31]);  // AND_Gate
  and and_8 (and_8_out, and_7_out, out_5[31]);
  and and_9 (and_9_out, or_4_out, and_11_out);
  and and_10 (and_10_out, A[31], ~B[31]);  // AND_Gate
  or or_4 (or_4_out, and_8_out, and_12_out);
  and and_11 (and_11_out, OP[0], OP[1], OP[2], ~OP[3]);  // AND_Gate
  and and_12 (and_12_out, and_10_out, ~out_5[31]);  // AND_Gate

  // Other names for the same wires on the sheet: S[31:0] = out_5
endmodule
