// Logisim project caminho_dados.circ as structural Verilog: 12 circuits, main circuit main
module main (
  input  CLEAR,
  input  in_2,
  input  CLEAR_2,
  input  REGWRITE,
  input  CLEAR_3
);

  wire and_1_out, BNE, BRANCH, EXCEPTION, EXCOUT, J, JR, LINK, MEMREAD, MEMTOREG, MEMWRITE, MTC0,
       multiplexer_3_out, not_1_out, REGDIST, ULASRC, ZERO;
  wire [1:0] CONTROLE_INSTRUCAO_ulaop;
  wire [3:0] OP;
  wire [4:0] DECODIFICADOR_rd, DECODIFICADOR_rs, DECODIFICADOR_rt, DECODIFICADOR_shamt, multiplexer_8_out,
       multiplexer_9_out, WR, WREXCEPT;
  wire [5:0] FUNCT, OPCODE;
  wire [15:0] DECODIFICADOR_imm;
  wire [31:0] adder_1_out, CONC__2, EPC, IMM32, LD1, LD2, MEMORIA_DADOS_instrucao,
       MEMORIA_INSTRUCAO_instrucao, MFC0R, multiplexer_1_out, multiplexer_2_out, multiplexer_4_out,
       multiplexer_5_out, multiplexer_6_out, multiplexer_7_out, multiplexer_11_out, multiplexer_12_out,
       multiplexer_13_out, multiplexer_14_out, PC_4, register_1_q, RESULTADO, undriven;

  Multiplexer #(.width(32)) multiplexer_1 (
    .in0(multiplexer_5_out), .in1(LD1), .out(multiplexer_1_out), .sel(JR));  // open: en
  Multiplexer #(.width(32)) multiplexer_2 (
    .in0(multiplexer_1_out), .in1(CONC__2), .out(multiplexer_2_out), .sel(J));  // open: en
  Multiplexer multiplexer_3 (.in0(ZERO), .in1(not_1_out), .out(multiplexer_3_out), .sel(BNE));  // open: en
  not not_1 (not_1_out, ZERO);
  Multiplexer #(.width(32)) multiplexer_4 (
    .in0(RESULTADO), .in1(LD1), .out(multiplexer_4_out), .sel(MTC0));  // open: en
  Multiplexer #(.width(32)) multiplexer_5 (
    .in0(PC_4), .in1(adder_1_out), .out(multiplexer_5_out), .sel(and_1_out));  // open: en
  and and_1 (and_1_out, multiplexer_3_out, BRANCH);
  Multiplexer #(.width(32)) multiplexer_6 (
    .in0(multiplexer_2_out), .in1(32'h80000180), .out(multiplexer_6_out), .sel(EXCEPTION));  // open: en
  Multiplexer #(.width(32)) multiplexer_7 (
    .in0(multiplexer_6_out), .in1(EPC), .out(multiplexer_7_out), .sel(EXCOUT));  // open: en
  Adder #(.width(32)) adder_1 (.a({IMM32[29:0], 2'b00}), .b(PC_4), .out(adder_1_out));  // open: cin, cout
  Register #(.width(32)) register_1 (.D(multiplexer_7_out), .en(1'b1), .Q(register_1_q), .clk(in_2), .clr(CLEAR));
  excessao EXCESSAO (
    .Exception(EXCEPTION), .EPC_in(PC_4), .Res_Data(multiplexer_4_out), .WR_in(WR), .Clock(in_2),
    .WriteRes__mtc0(MTC0), .EPC(EPC), .MFC0R(MFC0R), .WR_out(WREXCEPT));
  memoria_instrucao MEMORIA_INSTRUCAO (.endereco_instr(register_1_q), .instrucao(MEMORIA_INSTRUCAO_instrucao));
  conc CONC (.pc_4(undriven), .addr(PC_4), ._2(CONC__2));
  Adder #(.width(32)) adder_2 (.a(32'h4), .b(register_1_q), .out(PC_4));  // open: cin, cout
  decodificador DECODIFICADOR (
    .\Instrução (MEMORIA_INSTRUCAO_instrucao), .Funct(FUNCT), .RS(DECODIFICADOR_rs), .RT(DECODIFICADOR_rt),
    .RD(DECODIFICADOR_rd), .OP_code(OPCODE), .SHAMT(DECODIFICADOR_shamt), .addr(undriven[25:0]),
    .imm(DECODIFICADOR_imm));
  extensao_sinal EXTENSAO_SINAL (.in_1(DECODIFICADOR_imm), .out_2(IMM32));
  controle_instrucao CONTROLE_INSTRUCAO (
    .OPcode(MEMORIA_INSTRUCAO_instrucao[31:26]), .RegDst(REGDIST), .MemToReg(MEMTOREG),
    .ULAop(CONTROLE_INSTRUCAO_ulaop), .MemRead(MEMREAD), .MemWrite(MEMWRITE), .Branch(BRANCH), .BNE(BNE),
    .LINK(LINK), .ExcOut(EXCOUT), .MTC0(MTC0));  // open: in_2, ULASrc, RegWrite, JUMP, MFC0
  Multiplexer #(.width(5)) multiplexer_8 (
    .in0(DECODIFICADOR_rt), .in1(DECODIFICADOR_rd), .out(multiplexer_8_out), .sel(REGDIST));  // open: en
  Multiplexer #(.width(5)) multiplexer_9 (
    .in0(multiplexer_8_out), .in1(WREXCEPT), .out(multiplexer_9_out), .sel(EXCOUT));  // open: en
  Multiplexer #(.width(5)) multiplexer_10 (.in0(multiplexer_9_out), .in1({5{1'b1}}), .out(WR), .sel(LINK));  // open: en
  Multiplexer #(.width(32)) multiplexer_11 (
    .in0(multiplexer_12_out), .in1(MFC0R), .out(multiplexer_11_out), .sel(EXCOUT));  // open: en
  controle_ula CONTROLE_ULA (.funct(FUNCT), .ULAOp(CONTROLE_INSTRUCAO_ulaop), .jumpRegister(JR), .OP(OP));
  Multiplexer #(.width(32)) multiplexer_12 (
    .in0(RESULTADO), .in1(MEMORIA_DADOS_instrucao), .out(multiplexer_12_out), .sel(MEMTOREG));  // open: en
  registradores REGISTRADORES (
    .read_2(DECODIFICADOR_rt), .read_1(DECODIFICADOR_rs), .write_data(multiplexer_13_out),
    .write_register(WR), .clock(in_2), .clear(CLEAR_2), .regWrite(REGWRITE), .read_data_1(LD1),
    .read_data_2(LD2));  // open: out_9, out_8
  Multiplexer #(.width(32)) multiplexer_13 (
    .in0(multiplexer_11_out), .in1(PC_4), .out(multiplexer_13_out), .sel(LINK));  // open: en
  Multiplexer #(.width(32)) multiplexer_14 (
    .in0(LD2), .in1(IMM32), .out(multiplexer_14_out), .sel(ULASRC));  // open: en
  ula ULA (
    .A(LD1), .B(multiplexer_14_out), .OPERACAOULA(OP), .SHAMT(DECODIFICADOR_shamt), .ZERO(ZERO),
    .RESULTADO(RESULTADO), .Overflow(EXCEPTION));
  memoria_dados MEMORIA_DADOS (
    .EL(RESULTADO), .WD(LD2), .store(MEMWRITE), .CLK(in_2), .load(MEMREAD), .reset(CLEAR_3),
    .instrucao(MEMORIA_DADOS_instrucao));

  // Other names for the same wires on the sheet: CLK = in_2
endmodule

module controle_ula (
  input  [5:0] funct,
  input  [1:0] ULAOp,
  output jumpRegister,
  output [3:0] OP
);

  wire JR_out, R_out;

  Multiplexer #(.select(2), .width(4), .enable("false")) multiplexer_1 (
    .in0(funct[5:2]), .in1(4'b0110), .in2(4'b0111), .in3(4'b0000), .out(OP), .sel(ULAOp));
  and R (R_out, ~ULAOp[0], ~ULAOp[1]);  // AND_Gate
  and JR (JR_out, ~funct[0], ~funct[1], ~funct[2], funct[3], ~funct[4], ~funct[5]);  // AND_Gate
  and and_1 (jumpRegister, JR_out, R_out);

  // Notes on the sheet:
  //   JR: funct = 001000
endmodule

module controle_instrucao (
  input  [5:0] OPcode,
  input  in_2,
  output RegDst,
  output MemToReg,
  output ULASrc,
  output RegWrite,
  output [1:0] ULAop,
  output MemRead,
  output MemWrite,
  output Branch,
  output BNE,
  output JUMP,
  output LINK,
  output ExcOut,
  output MTC0,
  output MFC0
);

  wire ADDI_out, BEQ_out, J_out, not_1_out, not_2_out;
  wire [1:0] multiplexer_1_out;

  and R (RegDst, ~OPcode[0], ~OPcode[1], ~OPcode[2], ~OPcode[3], ~OPcode[4], ~OPcode[5]);  // AND_Gate
  and ADDI (ADDI_out, ~OPcode[0], ~OPcode[1], ~OPcode[2], OPcode[3], ~OPcode[4], ~OPcode[5]);  // AND_Gate
  and LW (MemRead, OPcode[0], OPcode[1], ~OPcode[2], ~OPcode[3], ~OPcode[4], OPcode[5]);  // AND_Gate
  and SW (MemWrite, OPcode[0], OPcode[1], ~OPcode[2], OPcode[3], ~OPcode[4], OPcode[5]);  // AND_Gate
  and BEQ (BEQ_out, ~OPcode[0], ~OPcode[1], OPcode[2], ~OPcode[3], ~OPcode[4]);  // AND_Gate
  and u_BNE (BNE, OPcode[0], ~OPcode[1], OPcode[2], ~OPcode[3], ~OPcode[4], ~OPcode[5]);  // AND_Gate
  and J (J_out, ~OPcode[0], OPcode[1], ~OPcode[2], ~OPcode[3], ~OPcode[4], ~OPcode[5]);  // AND_Gate
  and JAL (LINK, OPcode[0], OPcode[1], ~OPcode[2], ~OPcode[3], ~OPcode[4], ~OPcode[5]);  // AND_Gate
  and RFE (ExcOut, ~OPcode[0], ~OPcode[1], ~OPcode[2], ~OPcode[3], ~OPcode[4], OPcode[5]);  // AND_Gate
  and u_MTC0 (MTC0, ~OPcode[0], ~OPcode[1], ~OPcode[2], ~OPcode[3], OPcode[4], OPcode[5]);  // AND_Gate
  and u_MFC0 (MFC0, ~OPcode[0], ~OPcode[1], ~OPcode[2], OPcode[3], OPcode[4], OPcode[5]);  // AND_Gate
  not not_1 (not_1_out, RegDst);
  not not_2 (not_2_out, RegDst);
  or or_1 (MemToReg, not_1_out, MemRead);
  or or_2 (ULASrc, not_2_out, ADDI_out, MemRead, MemWrite);
  or or_3 (RegWrite, RegDst, ADDI_out, MemRead, LINK, MFC0);
  Multiplexer #(.width(2)) multiplexer_1 (.in0(2'b01), .in1(2'b00), .out(multiplexer_1_out), .sel(RegDst));  // open: en
  or or_4 (Branch, BEQ_out, BNE);
  or or_5 (JUMP, J_out, LINK);
  Multiplexer #(.width(2)) multiplexer_2 (.in0(multiplexer_1_out), .in1(2'b10), .out(ULAop), .sel(Branch));  // open: en

  // Other names for the same wires on the sheet: tipo_R = RegDst

  // Notes on the sheet:
  //   ativar ULAOp pra  imediatos
  //   WriteRegEx
endmodule

module extensao_sinal (
  input  [15:0] in_1,
  output [31:0] out_2
);


  assign out_2 = {{17{in_1[15]}}, in_1[14:0]};
endmodule

module ula (
  input  [31:0] A,
  input  [31:0] B,
  input  [3:0] OPERACAOULA,
  input  [4:0] SHAMT,
  output ZERO,
  output [31:0] RESULTADO,
  output Overflow
);

  wire and_1_out, and_2_out, and_3_out, and_4_out, comparator_1_gt, \Só_ADD_out , \Só_SUB_2_out ,
       \Só_SUB_out , xor_1_out, xor_2_out, xor_3_out, xor_4_out;
  wire [0:0] comparator_1_eq, comparator_1_lt;
  wire [31:0] _000_out, _001_out, _010_out, _011_out, adder_1_out, shifter_1_out, shifter_2_out,
       subtractor_1_out;

  assign _000_out = A & B;  // AND_Gate _000, 32 bits wide
  assign _001_out = A | B;  // OR_Gate _001, 32 bits wide
  assign _010_out = ~(A | B);  // NOR_Gate _010, 32 bits wide
  assign _011_out = A ^ B;  // XOR_Gate _011, 32 bits wide
  Comparator #(.width(32)) comparator_1 (
    .a(A), .b(B), .gt(comparator_1_gt), .eq(comparator_1_eq[0]), .lt(comparator_1_lt[0]));
  Adder #(.width(32)) adder_1 (.a(A), .b(B), .out(adder_1_out));  // open: cin, cout
  Subtractor #(.width(32)) subtractor_1 (.a(A), .b(B), .out(subtractor_1_out));  // open: bin, bout
  Shifter #(.width(32)) shifter_1 (.in(A), .\dist (SHAMT), .out(shifter_1_out));
  Shifter #(.width(32), .shift("lr")) shifter_2 (.in(A), .\dist (SHAMT), .out(shifter_2_out));
  Multiplexer #(.select(4), .width(32)) multiplexer_1 (
    .in0(_000_out), .in1(_001_out), .in2(_010_out), .in3(_011_out), .in4({{31{1'b0}}, comparator_1_eq[0]}),
    .in5({{31{1'b0}}, comparator_1_lt[0]}), .in6(adder_1_out), .in7(subtractor_1_out), .in8(shifter_1_out),
    .in9(shifter_2_out), .out(RESULTADO), .sel(OPERACAOULA));  // open: in10, in11, in12, in13, in14, in15, en
  nor nor_1 (ZERO, RESULTADO[31], RESULTADO[30], RESULTADO[29], RESULTADO[28], RESULTADO[27], RESULTADO[26], RESULTADO[25], RESULTADO[24], RESULTADO[23], RESULTADO[22], RESULTADO[21], RESULTADO[20], RESULTADO[19], RESULTADO[18], RESULTADO[17], RESULTADO[16], RESULTADO[15], RESULTADO[14], RESULTADO[13], RESULTADO[12], RESULTADO[11], RESULTADO[10], RESULTADO[9], RESULTADO[8], RESULTADO[7], RESULTADO[6], RESULTADO[5], RESULTADO[4], RESULTADO[3], RESULTADO[2], RESULTADO[1], RESULTADO[0]);
  xor xor_1 (xor_1_out, B[31], A[31]);
  xor xor_2 (xor_2_out, B[31], A[31]);
  and and_1 (and_1_out, B[31], A[31]);
  and \Só_SUB  (\Só_SUB_out , OPERACAOULA[0], OPERACAOULA[1], OPERACAOULA[2], ~OPERACAOULA[3]);  // AND_Gate
  and \Só_SUB_2  (\Só_SUB_2_out , OPERACAOULA[0], OPERACAOULA[1], OPERACAOULA[2], ~OPERACAOULA[3]);  // AND_Gate
  xor xor_3 (xor_3_out, RESULTADO[31], and_1_out);
  and \Só_ADD  (\Só_ADD_out , ~OPERACAOULA[0], OPERACAOULA[1], OPERACAOULA[2], ~OPERACAOULA[3]);  // AND_Gate
  and and_2 (and_2_out, ~RESULTADO[31], xor_1_out, \Só_SUB_out );  // AND_Gate
  xor xor_4 (xor_4_out, and_2_out, and_3_out);
  and and_3 (and_3_out, RESULTADO[31], xor_2_out, \Só_SUB_2_out );
  and and_4 (and_4_out, xor_3_out, \Só_ADD_out );
  or or_1 (Overflow, xor_4_out, and_4_out);

  // Other names for the same wires on the sheet: Operação_ALU[3:0] = OPERACAOULA

  // Notes on the sheet:
  //   CASOS OVERFLOW
  //   ADD overflow se:
  //   SUB overflow se:
  //   (+x)+ (+y) = - 
  //   	(-x)+ (-y) = +
  //   (-a) - (+b) =  + 
  //   (+a) - (-b) = - 
  //   100
  //   101
  //   110
  //   111
  //   1000
  //   1001
  //   Caso 1 Subtração
  //   Caso 2 Subtração
  //   Casos Adição
  //   MSB de Resultado
  //   MSB de Resultado
endmodule

module decodificador (
  input  [31:0] \Instrução ,
  output [5:0] Funct,
  output [4:0] RS,
  output [4:0] RT,
  output [4:0] RD,
  output [5:0] OP_code,
  output [4:0] SHAMT,
  output [25:0] addr,
  output [15:0] imm
);

  wire J_out, JAL_out, or_1_out, R_out;
  wire [9:0] I;
  wire [15:6] demultiplexer_2_out1;
  wire [25:0] \Não_R ;

  and R (R_out, ~\Instrução [26], ~\Instrução [27], ~\Instrução [28], ~\Instrução [29], ~\Instrução [30], ~\Instrução [31]);  // AND_Gate
  Demultiplexer #(.width(26), .enable("false")) demultiplexer_1 (
    .out0({imm, I}), .out1(addr), .in(\Não_R ), .sel(or_1_out));
  or or_1 (or_1_out, J_out, JAL_out);
  and J (J_out, ~\Instrução [26], ~\Instrução [27], ~\Instrução [28], ~\Instrução [29], \Instrução [30], ~\Instrução [31]);  // AND_Gate
  and JAL (JAL_out, ~\Instrução [26], ~\Instrução [27], ~\Instrução [28], ~\Instrução [29], \Instrução [30], \Instrução [31]);  // AND_Gate
  Demultiplexer #(.width(26), .enable("false")) demultiplexer_2 (
    .out0(\Não_R ), .out1({SHAMT, RD, demultiplexer_2_out1, Funct}),
    .in({\Instrução [0], \Instrução [1], \Instrução [2], \Instrução [3], \Instrução [4], \Instrução [5], \Instrução [6], \Instrução [7], \Instrução [8], \Instrução [9], \Instrução [10], \Instrução [11], \Instrução [12], \Instrução [13], \Instrução [14], \Instrução [15], \Instrução [16], \Instrução [17], \Instrução [18], \Instrução [19], \Instrução [20], \Instrução [21], \Instrução [22], \Instrução [23], \Instrução [24], \Instrução [25]}),
    .sel(R_out));
  assign RS = demultiplexer_2_out1[10:6] | I[4:0];  // OR_Gate or_2, 5 bits wide
  assign RT = demultiplexer_2_out1[15:11] | I[9:5];  // OR_Gate or_3, 5 bits wide

  assign OP_code = \Instrução [31:26];

  // Other names for the same wires on the sheet: I[25:10] = imm; J[25:0] = addr
endmodule

module registradores (
  input  [4:0] read_2,
  input  [4:0] read_1,
  input  [31:0] write_data,
  input  [4:0] write_register,
  input  clock,
  input  clear,
  input  regWrite,
  output [31:0] out_8,
  output [31:0] out_9,
  output [31:0] read_data_1,
  output [31:0] read_data_2
);

  wire we00, we01, we02, we03, we04, we05, we06, we07, we08, we09, we10, we11, we12, we13, we14, we15, we16,
       we17, we18, we19, we20, we21, we22, we23, we24, we25, we26, we27, we28, we29, we30, we31;
  wire [31:0] s00, s01, s02, s03, s04, s05, s06, s07, s08, s09, s10, s11, s12, s13, s14, s15, s16, s17, s18,
       s19, s20, s21, s22, s23, s24, s25, s26, s27, s28, s29, s30, s31, wd00, wd03, wd04, wd05, wd06, wd07,
       wd08, wd09, wd10, wd11, wd12, wd13, wd14, wd15, wd16, wd17, wd18, wd19, wd20, wd21, wd22, wd23, wd24,
       wd25, wd26, wd27, wd28, wd29, wd30, wd31;

  Demultiplexer #(.select(5)) demultiplexer_1 (
    .out0(we00), .out1(we01), .out2(we02), .out3(we03), .out4(we04), .out5(we05), .out6(we06), .out7(we07),
    .out8(we08), .out9(we09), .out10(we10), .out11(we11), .out12(we12), .out13(we13), .out14(we14),
    .out15(we15), .out16(we16), .out17(we17), .out18(we18), .out19(we19), .out20(we20), .out21(we21),
    .out22(we22), .out23(we23), .out24(we24), .out25(we25), .out26(we26), .out27(we27), .out28(we28),
    .out29(we29), .out30(we30), .out31(we31), .in(regWrite), .sel(write_register));  // open: en
  Demultiplexer #(.select(5), .width(32)) demultiplexer_2 (
    .out0(wd00), .out1(out_9), .out2(out_8), .out3(wd03), .out4(wd04), .out5(wd05), .out6(wd06), .out7(wd07),
    .out8(wd08), .out9(wd09), .out10(wd10), .out11(wd11), .out12(wd12), .out13(wd13), .out14(wd14),
    .out15(wd15), .out16(wd16), .out17(wd17), .out18(wd18), .out19(wd19), .out20(wd20), .out21(wd21),
    .out22(wd22), .out23(wd23), .out24(wd24), .out25(wd25), .out26(wd26), .out27(wd27), .out28(wd28),
    .out29(wd29), .out30(wd30), .out31(wd31), .in(write_data), .sel(write_register));  // open: en
  banco_registradoderes_register zero (
    .en(we00), .clear(clear), .clock(clock), .Entradas_D({32{1'b0}}), .Saidas_Q(s00));
  banco_registradoderes_register a0 (.en(we04), .clear(clear), .clock(clock), .Entradas_D(wd04), .Saidas_Q(s04));
  banco_registradoderes_register t0 (.en(we08), .clear(clear), .clock(clock), .Entradas_D(wd08), .Saidas_Q(s08));
  banco_registradoderes_register t4 (.en(we12), .clear(clear), .clock(clock), .Entradas_D(wd12), .Saidas_Q(s12));
  banco_registradoderes_register s0 (.en(we16), .clear(clear), .clock(clock), .Entradas_D(wd16), .Saidas_Q(s16));
  banco_registradoderes_register s4 (.en(we20), .clear(clear), .clock(clock), .Entradas_D(wd20), .Saidas_Q(s20));
  banco_registradoderes_register t8 (.en(we24), .clear(clear), .clock(clock), .Entradas_D(wd24), .Saidas_Q(s24));
  banco_registradoderes_register gp (.en(we28), .clear(clear), .clock(clock), .Entradas_D(wd28), .Saidas_Q(s28));
  banco_registradoderes_register at (.en(we01), .clear(clear), .clock(clock), .Entradas_D(out_9), .Saidas_Q(s01));
  banco_registradoderes_register a1 (.en(we05), .clear(clear), .clock(clock), .Entradas_D(wd05), .Saidas_Q(s05));
  banco_registradoderes_register t1 (.en(we09), .clear(clear), .clock(clock), .Entradas_D(wd09), .Saidas_Q(s09));
  banco_registradoderes_register t5 (.en(we13), .clear(clear), .clock(clock), .Entradas_D(wd13), .Saidas_Q(s13));
  banco_registradoderes_register s1 (.en(we17), .clear(clear), .clock(clock), .Entradas_D(wd17), .Saidas_Q(s17));
  banco_registradoderes_register s5 (.en(we21), .clear(clear), .clock(clock), .Entradas_D(wd21), .Saidas_Q(s21));
  banco_registradoderes_register t9 (.en(we25), .clear(clear), .clock(clock), .Entradas_D(wd25), .Saidas_Q(s25));
  banco_registradoderes_register sp (.en(we29), .clear(clear), .clock(clock), .Entradas_D(wd29), .Saidas_Q(s29));
  banco_registradoderes_register v0 (.en(we02), .clear(clear), .clock(clock), .Entradas_D(out_8), .Saidas_Q(s02));
  banco_registradoderes_register a2 (.en(we06), .clear(clear), .clock(clock), .Entradas_D(wd06), .Saidas_Q(s06));
  banco_registradoderes_register t2 (.en(we10), .clear(clear), .clock(clock), .Entradas_D(wd10), .Saidas_Q(s10));
  banco_registradoderes_register t6 (.en(we14), .clear(clear), .clock(clock), .Entradas_D(wd14), .Saidas_Q(s14));
  banco_registradoderes_register s2 (.en(we18), .clear(clear), .clock(clock), .Entradas_D(wd18), .Saidas_Q(s18));
  banco_registradoderes_register s6 (.en(we22), .clear(clear), .clock(clock), .Entradas_D(wd22), .Saidas_Q(s22));
  banco_registradoderes_register k0 (.en(we26), .clear(clear), .clock(clock), .Entradas_D(wd26), .Saidas_Q(s26));
  banco_registradoderes_register fp (.en(we30), .clear(clear), .clock(clock), .Entradas_D(wd30), .Saidas_Q(s30));
  banco_registradoderes_register v1 (.en(we03), .clear(clear), .clock(clock), .Entradas_D(wd03), .Saidas_Q(s03));
  banco_registradoderes_register a3 (.en(we07), .clear(clear), .clock(clock), .Entradas_D(wd07), .Saidas_Q(s07));
  banco_registradoderes_register t3 (.en(we11), .clear(clear), .clock(clock), .Entradas_D(wd11), .Saidas_Q(s11));
  banco_registradoderes_register t7 (.en(we15), .clear(clear), .clock(clock), .Entradas_D(wd15), .Saidas_Q(s15));
  banco_registradoderes_register s3 (.en(we19), .clear(clear), .clock(clock), .Entradas_D(wd19), .Saidas_Q(s19));
  banco_registradoderes_register s7 (.en(we23), .clear(clear), .clock(clock), .Entradas_D(wd23), .Saidas_Q(s23));
  banco_registradoderes_register k1 (.en(we27), .clear(clear), .clock(clock), .Entradas_D(wd27), .Saidas_Q(s27));
  banco_registradoderes_register ra (.en(we31), .clear(clear), .clock(clock), .Entradas_D(wd31), .Saidas_Q(s31));
  Multiplexer #(.select(5), .width(32)) multiplexer_1 (
    .in0(s00), .in1(s01), .in2(s02), .in3(s03), .in4(s04), .in5(s05), .in6(s06), .in7(s07), .in8(s08),
    .in9(s09), .in10(s10), .in11(s11), .in12(s12), .in13(s13), .in14(s14), .in15(s15), .in16(s16),
    .in17(s17), .in18(s18), .in19(s19), .in20(s20), .in21(s21), .in22(s22), .in23(s23), .in24(s24),
    .in25(s25), .in26(s26), .in27(s27), .in28(s28), .in29(s29), .in30(s30), .in31(s31), .out(read_data_1),
    .sel(read_1));  // open: en
  Multiplexer #(.select(5), .width(32)) multiplexer_2 (
    .in0(s00), .in1(s01), .in2(s02), .in3(s03), .in4(s04), .in5(s05), .in6(s06), .in7(s07), .in8(s08),
    .in9(s09), .in10(s10), .in11(s11), .in12(s12), .in13(s13), .in14(s14), .in15(s15), .in16(s16),
    .in17(s17), .in18(s18), .in19(s19), .in20(s20), .in21(s21), .in22(s22), .in23(s23), .in24(s24),
    .in25(s25), .in26(s26), .in27(s27), .in28(s28), .in29(s29), .in30(s30), .in31(s31), .out(read_data_2),
    .sel(read_2));  // open: en

  // Other names for the same wires on the sheet: wd01[31:0] = out_9; wd02[31:0] = out_8
endmodule

module memoria_dados (
  input  CLK,
  input  reset,
  input  store,
  input  load,
  input  [31:0] EL,
  input  [31:0] WD,
  output [31:0] instrucao
);

  RAM #(.addrWidth(24), .dataWidth(32), .bus("separate")) ram_1 (
    .addr(EL[25:2]), .din(WD), .data(instrucao), .str(store), .clk(CLK), .ld(load), .clr(reset));  // open: sel
endmodule

module memoria_instrucao (
  input  [31:0] endereco_instr,
  output [31:0] instrucao
);

  RAM #(.addrWidth(24), .dataWidth(32)) ram_1 (
    .addr(endereco_instr[25:2]), .data(instrucao), .ld(1'b1));  // open: sel, clk, clr
endmodule

module excessao (
  input  Exception,
  input  [31:0] EPC_in,
  input  [31:0] Res_Data,
  input  [4:0] WR_in,
  input  Clock,
  input  WriteRes__mtc0,
  output [31:0] EPC,
  output [31:0] MFC0R,
  output [4:0] WR_out
);

  wire or_1_out;

  Register #(.width(32)) u_EPC (.D(EPC_in), .en(Exception), .Q(EPC), .clk(Clock));  // open: clr
  Register #(.width(32)) Result (.D(Res_Data), .en(or_1_out), .Q(MFC0R), .clk(Clock));  // open: clr
  Register #(.width(5)) WR (.D(WR_in), .en(Exception), .Q(WR_out), .clk(Clock));  // open: clr
  or or_1 (or_1_out, Exception, WriteRes__mtc0);
endmodule

module register (
  input  en,
  input  clear,
  input  clock,
  input  [31:0] Entradas_D,
  output [31:0] Saidas_Q
);

  D_Flip_Flop _00 (.clk(clock), .D(Entradas_D[0]), .Q(Saidas_Q[0]), .en(en), .reset(clear));  // open: Qn, preset
  D_Flip_Flop _01 (.clk(clock), .D(Entradas_D[1]), .Q(Saidas_Q[1]), .reset(clear));  // open: Qn, preset, en
  D_Flip_Flop _02 (.clk(clock), .D(Entradas_D[2]), .Q(Saidas_Q[2]), .reset(clear));  // open: Qn, preset, en
  D_Flip_Flop _03 (.clk(clock), .D(Entradas_D[3]), .Q(Saidas_Q[3]), .reset(clear));  // open: Qn, preset, en
  D_Flip_Flop _04 (.clk(clock), .D(Entradas_D[4]), .Q(Saidas_Q[4]), .reset(clear));  // open: Qn, preset, en
  D_Flip_Flop _05 (.clk(clock), .D(Entradas_D[5]), .Q(Saidas_Q[5]), .reset(clear));  // open: Qn, preset, en
  D_Flip_Flop _06 (.clk(clock), .D(Entradas_D[6]), .Q(Saidas_Q[6]), .reset(clear));  // open: Qn, preset, en
  D_Flip_Flop _07 (.clk(clock), .D(Entradas_D[7]), .Q(Saidas_Q[7]), .reset(clear));  // open: Qn, preset, en
  D_Flip_Flop _08 (.clk(clock), .D(Entradas_D[8]), .Q(Saidas_Q[8]), .en(en), .reset(clear));  // open: Qn, preset
  D_Flip_Flop _09 (.clk(clock), .D(Entradas_D[9]), .Q(Saidas_Q[9]), .en(en), .reset(clear));  // open: Qn, preset
  D_Flip_Flop _10 (.clk(clock), .D(Entradas_D[10]), .Q(Saidas_Q[10]), .en(en), .reset(clear));  // open: Qn, preset
  D_Flip_Flop _11 (.clk(clock), .D(Entradas_D[11]), .Q(Saidas_Q[11]), .en(en), .reset(clear));  // open: Qn, preset
  D_Flip_Flop _12 (.clk(clock), .D(Entradas_D[12]), .Q(Saidas_Q[12]), .en(en), .reset(clear));  // open: Qn, preset
  D_Flip_Flop _13 (.clk(clock), .D(Entradas_D[13]), .Q(Saidas_Q[13]), .en(en), .reset(clear));  // open: Qn, preset
  D_Flip_Flop _14 (.clk(clock), .D(Entradas_D[14]), .Q(Saidas_Q[14]), .en(en), .reset(clear));  // open: Qn, preset
  D_Flip_Flop _15 (.clk(clock), .D(Entradas_D[15]), .Q(Saidas_Q[15]), .en(en), .reset(clear));  // open: Qn, preset
  D_Flip_Flop _16 (.clk(clock), .D(Entradas_D[16]), .Q(Saidas_Q[16]), .en(en), .reset(clear));  // open: Qn, preset
  D_Flip_Flop _17 (.clk(clock), .D(Entradas_D[17]), .Q(Saidas_Q[17]), .en(en), .reset(clear));  // open: Qn, preset
  D_Flip_Flop _18 (.clk(clock), .D(Entradas_D[18]), .Q(Saidas_Q[18]), .en(en), .reset(clear));  // open: Qn, preset
  D_Flip_Flop _19 (.clk(clock), .D(Entradas_D[19]), .Q(Saidas_Q[19]), .en(en), .reset(clear));  // open: Qn, preset
  D_Flip_Flop _20 (.clk(clock), .D(Entradas_D[20]), .Q(Saidas_Q[20]), .en(en), .reset(clear));  // open: Qn, preset
  D_Flip_Flop _21 (.clk(clock), .D(Entradas_D[21]), .Q(Saidas_Q[21]), .en(en), .reset(clear));  // open: Qn, preset
  D_Flip_Flop _22 (.clk(clock), .D(Entradas_D[22]), .Q(Saidas_Q[22]), .en(en), .reset(clear));  // open: Qn, preset
  D_Flip_Flop _23 (.clk(clock), .D(Entradas_D[23]), .Q(Saidas_Q[23]), .reset(clear));  // open: Qn, preset, en
  D_Flip_Flop _24 (.clk(clock), .D(Entradas_D[24]), .Q(Saidas_Q[24]), .en(en), .reset(clear));  // open: Qn, preset
  D_Flip_Flop _25 (.clk(clock), .D(Entradas_D[25]), .Q(Saidas_Q[25]), .en(en), .reset(clear));  // open: Qn, preset
  D_Flip_Flop _26 (.clk(clock), .D(Entradas_D[26]), .Q(Saidas_Q[26]), .en(en), .reset(clear));  // open: Qn, preset
  D_Flip_Flop _27 (.clk(clock), .D(Entradas_D[27]), .Q(Saidas_Q[27]), .en(en), .reset(clear));  // open: Qn, preset
  D_Flip_Flop _28 (.clk(clock), .D(Entradas_D[28]), .Q(Saidas_Q[28]), .en(en), .reset(clear));  // open: Qn, preset
  D_Flip_Flop _29 (.clk(clock), .D(Entradas_D[29]), .Q(Saidas_Q[29]), .en(en), .reset(clear));  // open: Qn, preset
  D_Flip_Flop _30 (.clk(clock), .D(Entradas_D[30]), .Q(Saidas_Q[30]), .reset(clear));  // open: Qn, preset, en
  D_Flip_Flop _31 (.clk(clock), .D(Entradas_D[31]), .Q(Saidas_Q[31]), .en(en), .reset(clear));  // open: Qn, preset

  // Notes on the sheet:
  //   REGISTRADOR FORMADO POR 32 FLIP-FLOPS D
  //   CIRCUITO DE UM REGISTRADOR
endmodule

module conc (
  input  [31:0] pc_4,
  input  [31:0] addr,
  output [31:0] _2
);


  assign _2 = {pc_4[22], pc_4[23], pc_4[24], pc_4[25], addr[25:0], 2'b00};
endmodule
