// Logisim project mem.circ as structural Verilog: 5 circuits, main circuit mem_dados
module mem_dados (
  input  memWrite,
  input  [31:0] EL,
  input  memRead,
  input  [31:0] WD,
  input  memRead_2,
  output [31:0] LD
);

  wire and_1_out, and_2_out, and_3_out, and_4_out, and_5_out, and_6_out, and_7_out, and_8_out, and_9_out,
       and_10_out, and_11_out, and_12_out, and_13_out, and_14_out, and_15_out, and_16_out, and_17_out,
       and_18_out, and_19_out, and_20_out, and_21_out, and_22_out, and_23_out, and_24_out, and_25_out,
       and_26_out, and_27_out, and_28_out, and_29_out, and_30_out, and_31_out, and_32_out, latch00_q,
       latch01_q, latch02_q, latch03_q, latch04_q, latch05_q, latch06_q, latch07_q, latch08_q, latch09_q,
       latch10_q, latch11_q, latch12_q, latch13_q, latch14_q, latch15_q, latch16_q, latch17_q, latch18_q,
       latch19_q, latch20_q, latch21_q, latch22_q, latch23_q, latch24_q, latch25_q, latch26_q, latch27_q,
       latch28_q, latch29_q, latch30_q, latch31_q, LOAD_STORY, or_1_out;

  or or_1 (or_1_out, memWrite, memRead_2);
  xor xor_1 (LOAD_STORY, or_1_out, memRead_2);
  and and_1 (and_1_out, EL[0], LOAD_STORY);
  and and_2 (and_2_out, EL[4], LOAD_STORY);
  and and_3 (and_3_out, EL[8], LOAD_STORY);
  and and_4 (and_4_out, EL[12], LOAD_STORY);
  and and_5 (and_5_out, EL[16], LOAD_STORY);
  and and_6 (and_6_out, EL[20], LOAD_STORY);
  and and_7 (and_7_out, 1'b1, LOAD_STORY);
  and and_8 (and_8_out, 1'b1, LOAD_STORY);
  assign LD[0] = EL[0] ? latch00_q : 1'bz;  // Controlled_Buffer controlled_buffer_1
  latch_D latch00 (.E(and_1_out), .D(WD[0]), .clear(memRead), .Q(latch00_q));  // open: Q_2
  assign LD[4] = EL[4] ? latch04_q : 1'bz;  // Controlled_Buffer controlled_buffer_2
  latch_D latch04 (.E(and_2_out), .D(WD[4]), .Q(latch04_q));  // open: clear, Q_2
  assign LD[8] = EL[8] ? latch08_q : 1'bz;  // Controlled_Buffer controlled_buffer_3
  latch_D latch08 (.E(and_3_out), .D(WD[8]), .Q(latch08_q));  // open: clear, Q_2
  latch_D latch12 (.E(and_4_out), .D(WD[12]), .Q(latch12_q));  // open: clear, Q_2
  assign LD[12] = EL[12] ? latch12_q : 1'bz;  // Controlled_Buffer controlled_buffer_4
  assign LD[16] = EL[16] ? latch16_q : 1'bz;  // Controlled_Buffer controlled_buffer_5
  latch_D latch16 (.E(and_5_out), .D(WD[16]), .Q(latch16_q));  // open: clear, Q_2
  assign LD[20] = EL[20] ? latch20_q : 1'bz;  // Controlled_Buffer controlled_buffer_6
  latch_D latch20 (.E(and_6_out), .D(WD[20]), .Q(latch20_q));  // open: clear, Q_2
  latch_D latch24 (.E(and_7_out), .D(WD[24]), .Q(latch24_q));  // open: clear, Q_2
  assign LD[24] = 1'b1 ? latch24_q : 1'bz;  // Controlled_Buffer controlled_buffer_7
  assign LD[28] = 1'b1 ? latch28_q : 1'bz;  // Controlled_Buffer controlled_buffer_8
  latch_D latch28 (.E(and_8_out), .D(WD[28]), .Q(latch28_q));  // open: clear, Q_2
  and and_9 (and_9_out, EL[1], LOAD_STORY);
  latch_D latch01 (.E(and_9_out), .D(WD[1]), .Q(latch01_q));  // open: clear, Q_2
  and and_10 (and_10_out, EL[5], LOAD_STORY);
  latch_D latch05 (.E(and_10_out), .D(WD[5]), .Q(latch05_q));  // open: clear, Q_2
  and and_11 (and_11_out, EL[9], LOAD_STORY);
  latch_D latch09 (.E(and_11_out), .D(WD[9]), .Q(latch09_q));  // open: clear, Q_2
  and and_12 (and_12_out, EL[13], LOAD_STORY);
  latch_D latch13 (.E(and_12_out), .D(WD[13]), .Q(latch13_q));  // open: clear, Q_2
  and and_13 (and_13_out, EL[17], LOAD_STORY);
  latch_D latch17 (.E(and_13_out), .D(WD[17]), .Q(latch17_q));  // open: clear, Q_2
  and and_14 (and_14_out, EL[21], LOAD_STORY);
  latch_D latch21 (.E(and_14_out), .D(WD[21]), .Q(latch21_q));  // open: clear, Q_2
  and and_15 (and_15_out, 1'b1, LOAD_STORY);
  latch_D latch25 (.E(and_15_out), .D(WD[25]), .Q(latch25_q));  // open: clear, Q_2
  and and_16 (and_16_out, 1'b1, LOAD_STORY);
  latch_D latch29 (.E(and_16_out), .D(WD[29]), .Q(latch29_q));  // open: clear, Q_2
  assign LD[1] = EL[1] ? latch01_q : 1'bz;  // Controlled_Buffer controlled_buffer_9
  assign LD[5] = EL[5] ? latch05_q : 1'bz;  // Controlled_Buffer controlled_buffer_10
  assign LD[9] = EL[9] ? latch09_q : 1'bz;  // Controlled_Buffer controlled_buffer_11
  assign LD[13] = EL[13] ? latch13_q : 1'bz;  // Controlled_Buffer controlled_buffer_12
  assign LD[17] = EL[17] ? latch17_q : 1'bz;  // Controlled_Buffer controlled_buffer_13
  assign LD[21] = EL[21] ? latch21_q : 1'bz;  // Controlled_Buffer controlled_buffer_14
  assign LD[25] = 1'b1 ? latch25_q : 1'bz;  // Controlled_Buffer controlled_buffer_15
  assign LD[29] = 1'b1 ? latch29_q : 1'bz;  // Controlled_Buffer controlled_buffer_16
  and and_17 (and_17_out, EL[2], LOAD_STORY);
  and and_18 (and_18_out, EL[6], LOAD_STORY);
  and and_19 (and_19_out, EL[10], LOAD_STORY);
  and and_20 (and_20_out, EL[14], LOAD_STORY);
  and and_21 (and_21_out, EL[18], LOAD_STORY);
  and and_22 (and_22_out, EL[22], LOAD_STORY);
  and and_23 (and_23_out, 1'b1, LOAD_STORY);
  and and_24 (and_24_out, 1'b1, LOAD_STORY);
  latch_D latch02 (.E(and_17_out), .D(WD[2]), .Q(latch02_q));  // open: clear, Q_2
  assign LD[2] = EL[2] ? latch02_q : 1'bz;  // Controlled_Buffer controlled_buffer_17
  assign LD[6] = EL[6] ? latch06_q : 1'bz;  // Controlled_Buffer controlled_buffer_18
  latch_D latch06 (.E(and_18_out), .D(WD[6]), .Q(latch06_q));  // open: clear, Q_2
  assign LD[10] = EL[10] ? latch10_q : 1'bz;  // Controlled_Buffer controlled_buffer_19
  latch_D latch10 (.E(and_19_out), .D(WD[10]), .Q(latch10_q));  // open: clear, Q_2
  assign LD[14] = EL[14] ? latch14_q : 1'bz;  // Controlled_Buffer controlled_buffer_20
  latch_D latch14 (.E(and_20_out), .D(WD[14]), .Q(latch14_q));  // open: clear, Q_2
  latch_D latch18 (.E(and_21_out), .D(WD[18]), .Q(latch18_q));  // open: clear, Q_2
  assign LD[18] = EL[18] ? latch18_q : 1'bz;  // Controlled_Buffer controlled_buffer_21
  assign LD[22] = EL[22] ? latch22_q : 1'bz;  // Controlled_Buffer controlled_buffer_22
  latch_D latch22 (.E(and_22_out), .D(WD[22]), .Q(latch22_q));  // open: clear, Q_2
  latch_D latch26 (.E(and_23_out), .D(WD[26]), .Q(latch26_q));  // open: clear, Q_2
  assign LD[26] = 1'b1 ? latch26_q : 1'bz;  // Controlled_Buffer controlled_buffer_23
  latch_D latch30 (.E(and_24_out), .D(WD[30]), .Q(latch30_q));  // open: clear, Q_2
  assign LD[30] = 1'b1 ? latch30_q : 1'bz;  // Controlled_Buffer controlled_buffer_24
  and and_25 (and_25_out, EL[3], LOAD_STORY);
  and and_26 (and_26_out, EL[7], LOAD_STORY);
  and and_27 (and_27_out, EL[11], LOAD_STORY);
  and and_28 (and_28_out, EL[15], LOAD_STORY);
  and and_29 (and_29_out, EL[19], LOAD_STORY);
  and and_30 (and_30_out, EL[23], LOAD_STORY);
  and and_31 (and_31_out, 1'b1, LOAD_STORY);
  and and_32 (and_32_out, 1'b1, LOAD_STORY);
  assign LD[3] = EL[3] ? latch03_q : 1'bz;  // Controlled_Buffer controlled_buffer_25
  latch_D latch03 (.E(and_25_out), .D(WD[3]), .Q(latch03_q));  // open: clear, Q_2
  assign LD[7] = EL[7] ? latch07_q : 1'bz;  // Controlled_Buffer controlled_buffer_26
  latch_D latch07 (.E(and_26_out), .D(WD[7]), .Q(latch07_q));  // open: clear, Q_2
  latch_D latch11 (.E(and_27_out), .D(WD[11]), .Q(latch11_q));  // open: clear, Q_2
  assign LD[11] = EL[11] ? latch11_q : 1'bz;  // Controlled_Buffer controlled_buffer_27
  assign LD[15] = EL[15] ? latch15_q : 1'bz;  // Controlled_Buffer controlled_buffer_28
  latch_D latch15 (.E(and_28_out), .D(WD[15]), .Q(latch15_q));  // open: clear, Q_2
  assign LD[19] = EL[19] ? latch19_q : 1'bz;  // Controlled_Buffer controlled_buffer_29
  latch_D latch19 (.E(and_29_out), .D(WD[19]), .Q(latch19_q));  // open: clear, Q_2
  assign LD[23] = EL[23] ? latch23_q : 1'bz;  // Controlled_Buffer controlled_buffer_30
  latch_D latch23 (.E(and_30_out), .D(WD[23]), .Q(latch23_q));  // open: clear, Q_2
  assign LD[27] = 1'b1 ? latch27_q : 1'bz;  // Controlled_Buffer controlled_buffer_31
  latch_D latch27 (.E(and_31_out), .D(WD[27]), .Q(latch27_q));  // open: clear, Q_2
  assign LD[31] = 1'b1 ? latch31_q : 1'bz;  // Controlled_Buffer controlled_buffer_32
  latch_D latch31 (.E(and_32_out), .D(WD[31]), .Q(latch31_q));  // open: clear, Q_2

  // Other names for the same wires on the sheet: E00 = EL[0]; E01 = EL[1]; E02 = EL[2]; E03 = EL[3]; E04 = EL[4];
  //   E05 = EL[5]; E06 = EL[6]; E07 = EL[7]; E08 = EL[8]; E09 = EL[9]; E10 = EL[10]; E11 = EL[11]; E12 = EL[12];
  //   E13 = EL[13]; E14 = EL[14]; E15 = EL[15]; E16 = EL[16]; E17 = EL[17]; E18 = EL[18]; E19 = EL[19]; E20 = EL[20];
  //   E21 = EL[21]; E22 = EL[22]; E23 = EL[23]; D00 = WD[0]; D01 = WD[1]; D02 = WD[2]; D03 = WD[3]; D04 = WD[4];
  //   D05 = WD[5]; D06 = WD[6]; D07 = WD[7]; D08 = WD[8]; D09 = WD[9]; D10 = WD[10]; D11 = WD[11]; D12 = WD[12];
  //   D13 = WD[13]; D14 = WD[14]; D15 = WD[15]; D16 = WD[16]; D17 = WD[17]; D18 = WD[18]; D19 = WD[19]; D20 = WD[20];
  //   D21 = WD[21]; D22 = WD[22]; D23 = WD[23]; D24 = WD[24]; D25 = WD[25]; D26 = WD[26]; D27 = WD[27]; D28 = WD[28];
  //   D29 = WD[29]; D30 = WD[30]; D31 = WD[31]
endmodule

module mem_instrucoes (
  input  CLK,
  input  reset,
  input  [31:0] endereco_instr,
  output [31:0] instrucao
);

  wire [31:0] ram_1_data;

  Register #(.width(32)) micro_instru (.D(ram_1_data), .Q(instrucao), .clk(CLK), .clr(reset));  // open: en
  RAM #(.addrWidth(24), .dataWidth(32)) ram_1 (
    .addr(endereco_instr[25:2]), .data(ram_1_data), .ld(1'b1));  // open: sel, clk, clr
endmodule

// Latch
module latch_D (
  input  E,
  input  D,
  input  clear,
  output Q,
  output Q_2
);

  wire and_1_out, and_2_out, nor_1_out, nor_2_out, not_1_out, not_2_out;

  not not_1 (not_1_out, D);
  and and_1 (and_1_out, not_1_out, E);
  and and_2 (and_2_out, E, D);
  nor nor_1 (nor_1_out, and_1_out, nor_2_out);
  nor nor_2 (nor_2_out, nor_1_out, and_2_out);
  not not_2 (not_2_out, clear);
  and and_3 (Q, nor_1_out, not_2_out);
  and and_4 (Q_2, nor_2_out, not_2_out);
endmodule

module mem_dados_ram (
  input  CLK,
  input  reset,
  input  store,
  input  load,
  input  [31:0] EL,
  input  [31:0] WD,
  output [31:0] instrucao
);

  RAM #(.addrWidth(24), .dataWidth(32), .bus("separate")) ram_1 (
    .addr(EL[25:2]), .din(WD), .data(instrucao), .str(store), .clk(CLK), .ld(load), .clr(reset));  // open: sel
endmodule

module mem (
  input  [31:0] in_1
);

  wire [31:0] and_1_out, and_2_out, and_3_out, and_4_out, and_5_out, and_6_out, and_7_out, and_8_out,
       and_9_out, and_10_out, and_11_out, and_12_out, and_13_out, and_14_out, and_15_out, and_16_out,
       and_17_out, and_18_out, and_19_out, and_20_out, and_21_out, and_22_out, and_23_out, and_24_out,
       and_25_out, and_26_out, and_27_out, and_28_out, and_29_out, and_30_out, and_31_out, and_32_out,
       and_33_out, and_34_out, and_35_out, and_36_out, and_37_out, and_38_out, and_39_out, and_40_out,
       and_41_out, and_42_out, and_43_out, and_44_out, and_47_out, and_50_out, and_51_out, and_52_out,
       and_53_out, and_54_out, undriven, undriven_2, undriven_3, undriven_4, undriven_5;

  // AND_Gate and_1 has open pins: out=and_1_out
  // AND_Gate and_2 has open pins: out=and_2_out
  // AND_Gate and_3 has open pins: out=and_3_out
  // AND_Gate and_4 has open pins: out=and_4_out
  // AND_Gate and_5 has open pins: out=and_5_out
  // AND_Gate and_6 has open pins: out=and_6_out
  // AND_Gate and_7 has open pins: out=and_7_out
  // AND_Gate and_8 has open pins: out=and_8_out
  // AND_Gate and_9 has open pins: out=and_9_out
  // AND_Gate and_10 has open pins: out=and_10_out
  // AND_Gate and_11 has open pins: out=and_11_out
  // AND_Gate and_12 has open pins: out=and_12_out
  // AND_Gate and_13 has open pins: out=and_13_out
  // AND_Gate and_14 has open pins: out=and_14_out
  // AND_Gate and_15 has open pins: out=and_15_out
  // AND_Gate and_16 has open pins: out=and_16_out
  // AND_Gate and_17 has open pins: out=and_17_out
  // AND_Gate and_18 has open pins: out=and_18_out
  // AND_Gate and_19 has open pins: out=and_19_out
  // AND_Gate and_20 has open pins: out=and_20_out
  // AND_Gate and_21 has open pins: out=and_21_out
  // AND_Gate and_22 has open pins: out=and_22_out
  // AND_Gate and_23 has open pins: out=and_23_out
  // AND_Gate and_24 has open pins: out=and_24_out
  // AND_Gate and_25 has open pins: out=and_25_out
  // AND_Gate and_26 has open pins: out=and_26_out
  // AND_Gate and_27 has open pins: out=and_27_out
  // AND_Gate and_28 has open pins: out=and_28_out
  // AND_Gate and_29 has open pins: out=and_29_out
  // AND_Gate and_30 has open pins: out=and_30_out
  // AND_Gate and_31 has open pins: out=and_31_out
  // AND_Gate and_32 has open pins: out=and_32_out
  // AND_Gate and_33 has open pins: out=and_33_out
  // AND_Gate and_34 has open pins: out=and_34_out
  // AND_Gate and_35 has open pins: out=and_35_out
  // AND_Gate and_36 has open pins: out=and_36_out
  // AND_Gate and_37 has open pins: out=and_37_out
  // AND_Gate and_38 has open pins: out=and_38_out
  // AND_Gate and_39 has open pins: out=and_39_out
  // AND_Gate and_40 has open pins: out=and_40_out
  // AND_Gate and_41 has open pins: out=and_41_out
  // AND_Gate and_42 has open pins: out=and_42_out
  // AND_Gate and_43 has open pins: out=and_43_out
  // AND_Gate and_44 has open pins: out=and_44_out
  // AND_Gate and_45 is placed but not wired
  // AND_Gate and_46 is placed but not wired
  // AND_Gate and_47 has open pins: out=and_47_out
  // AND_Gate and_48 is placed but not wired
  // AND_Gate and_49 is placed but not wired
  // AND_Gate and_50 has open pins: out=and_50_out
  // AND_Gate and_51 has open pins: out=and_51_out
  // AND_Gate and_52 has open pins: out=and_52_out
  // AND_Gate and_53 has open pins: out=and_53_out
  // AND_Gate and_54 has open pins: out=and_54_out
  // AND_Gate and_55 is placed but not wired
  // AND_Gate and_56 is placed but not wired
  // AND_Gate and_57 is placed but not wired
  // AND_Gate and_58 is placed but not wired
  // AND_Gate and_59 is placed but not wired
  // AND_Gate and_60 is placed but not wired
  // AND_Gate and_61 is placed but not wired
  // AND_Gate and_62 is placed but not wired
  // AND_Gate and_63 is placed but not wired
  // AND_Gate and_64 is placed but not wired
  // AND_Gate and_65 is placed but not wired
  // AND_Gate and_66 is placed but not wired
  // AND_Gate and_67 is placed but not wired
  // AND_Gate and_68 is placed but not wired
  // AND_Gate and_69 is placed but not wired
  // AND_Gate and_70 is placed but not wired
  // AND_Gate and_71 is placed but not wired
  // AND_Gate and_72 is placed but not wired
  // AND_Gate and_73 is placed but not wired
  // AND_Gate and_74 is placed but not wired
  // AND_Gate and_75 is placed but not wired
  // AND_Gate and_76 is placed but not wired
  // AND_Gate and_77 is placed but not wired
  // AND_Gate and_78 is placed but not wired
  // AND_Gate and_79 is placed but not wired
  // AND_Gate and_80 is placed but not wired
  // AND_Gate and_81 is placed but not wired
  // AND_Gate and_82 is placed but not wired
  // AND_Gate and_83 is placed but not wired
  // AND_Gate and_84 is placed but not wired
  // AND_Gate and_85 is placed but not wired
  // AND_Gate and_86 is placed but not wired
  // AND_Gate and_87 is placed but not wired
  // AND_Gate and_88 is placed but not wired
  // AND_Gate and_89 is placed but not wired
  // AND_Gate and_90 is placed but not wired
  // AND_Gate and_91 is placed but not wired
  // AND_Gate and_92 is placed but not wired
  // AND_Gate and_93 is placed but not wired
  // AND_Gate and_94 is placed but not wired
  // AND_Gate and_95 is placed but not wired
  // AND_Gate and_96 is placed but not wired
  // AND_Gate and_97 is placed but not wired
  // AND_Gate and_98 is placed but not wired
  // AND_Gate and_99 is placed but not wired
  // AND_Gate and_100 is placed but not wired
  // AND_Gate and_101 is placed but not wired
  // AND_Gate and_102 is placed but not wired
  // AND_Gate and_103 is placed but not wired
  // AND_Gate and_104 is placed but not wired
  // AND_Gate and_105 is placed but not wired
  // AND_Gate and_106 is placed but not wired
  // AND_Gate and_107 is placed but not wired
  // AND_Gate and_108 is placed but not wired
  // AND_Gate and_109 is placed but not wired
  // AND_Gate and_110 is placed but not wired
  // AND_Gate and_111 is placed but not wired
  // AND_Gate and_112 is placed but not wired
  // AND_Gate and_113 is placed but not wired
  // AND_Gate and_114 is placed but not wired
  // AND_Gate and_115 is placed but not wired
  // AND_Gate and_116 is placed but not wired
  // AND_Gate and_117 is placed but not wired
  // AND_Gate and_118 is placed but not wired
  // AND_Gate and_119 is placed but not wired
  // AND_Gate and_120 is placed but not wired
  // AND_Gate and_121 is placed but not wired
  // AND_Gate and_122 is placed but not wired
  // AND_Gate and_123 is placed but not wired
  // AND_Gate and_124 is placed but not wired
  // AND_Gate and_125 is placed but not wired
  // AND_Gate and_126 is placed but not wired
  // AND_Gate and_127 is placed but not wired
  // AND_Gate and_128 is placed but not wired
  // AND_Gate and_129 is placed but not wired
  // AND_Gate and_130 is placed but not wired
  // AND_Gate and_131 is placed but not wired
  // AND_Gate and_132 is placed but not wired
  // AND_Gate and_133 is placed but not wired
  // AND_Gate and_134 is placed but not wired
  // AND_Gate and_135 is placed but not wired
  // AND_Gate and_136 is placed but not wired
  // AND_Gate and_137 is placed but not wired
  // AND_Gate and_138 is placed but not wired
  // AND_Gate and_139 is placed but not wired
  // AND_Gate and_140 is placed but not wired
  // AND_Gate and_141 is placed but not wired
  // AND_Gate and_142 is placed but not wired
  // AND_Gate and_143 is placed but not wired
  // AND_Gate and_144 is placed but not wired
  // AND_Gate and_145 is placed but not wired
  // AND_Gate and_146 is placed but not wired
  // AND_Gate and_147 is placed but not wired
  // AND_Gate and_148 is placed but not wired
  // AND_Gate and_149 is placed but not wired
  // AND_Gate and_150 is placed but not wired
  // AND_Gate and_151 is placed but not wired
  // AND_Gate and_152 is placed but not wired
  // AND_Gate and_153 is placed but not wired
  // AND_Gate and_154 is placed but not wired
  // AND_Gate and_155 is placed but not wired
  // AND_Gate and_156 is placed but not wired
  // AND_Gate and_157 is placed but not wired
  // AND_Gate and_158 is placed but not wired
  // AND_Gate and_159 is placed but not wired
  // AND_Gate and_160 is placed but not wired
  // AND_Gate and_161 is placed but not wired
  // AND_Gate and_162 is placed but not wired
  // AND_Gate and_163 is placed but not wired
  // AND_Gate and_164 is placed but not wired
  // AND_Gate and_165 is placed but not wired
  // AND_Gate and_166 is placed but not wired
  // AND_Gate and_167 is placed but not wired
  // AND_Gate and_168 is placed but not wired
  // AND_Gate and_169 is placed but not wired
  // AND_Gate and_170 is placed but not wired
  // AND_Gate and_171 is placed but not wired
  // AND_Gate and_172 is placed but not wired
  // AND_Gate and_173 is placed but not wired
  // AND_Gate and_174 is placed but not wired
  // AND_Gate and_175 is placed but not wired
  // AND_Gate and_176 is placed but not wired
  // AND_Gate and_177 is placed but not wired
  // AND_Gate and_178 is placed but not wired
  // AND_Gate and_179 is placed but not wired
  // AND_Gate and_180 is placed but not wired
  // AND_Gate and_181 is placed but not wired
  // AND_Gate and_182 is placed but not wired
  // AND_Gate and_183 is placed but not wired
  // AND_Gate and_184 is placed but not wired
  // AND_Gate and_185 is placed but not wired
  // AND_Gate and_186 is placed but not wired
  // AND_Gate and_187 is placed but not wired
  // AND_Gate and_188 is placed but not wired
  // AND_Gate and_189 is placed but not wired
  // AND_Gate and_190 is placed but not wired
  // AND_Gate and_191 is placed but not wired
  // AND_Gate and_192 is placed but not wired
  // AND_Gate and_193 is placed but not wired
  // AND_Gate and_194 is placed but not wired
  // AND_Gate and_195 is placed but not wired
  // AND_Gate and_196 is placed but not wired
  // AND_Gate and_197 is placed but not wired
  // AND_Gate and_198 is placed but not wired
  // AND_Gate and_199 is placed but not wired
  // AND_Gate and_200 is placed but not wired
  // AND_Gate and_201 is placed but not wired
  // AND_Gate and_202 is placed but not wired
  // AND_Gate and_203 is placed but not wired
  // AND_Gate and_204 is placed but not wired
  // AND_Gate and_205 is placed but not wired
  // AND_Gate and_206 is placed but not wired
  // AND_Gate and_207 is placed but not wired
  // AND_Gate and_208 is placed but not wired
  // AND_Gate and_209 is placed but not wired
  // AND_Gate and_210 is placed but not wired
  // AND_Gate and_211 is placed but not wired
  // AND_Gate and_212 is placed but not wired
  // AND_Gate and_213 is placed but not wired
  // AND_Gate and_214 is placed but not wired
  // AND_Gate and_215 is placed but not wired
  // AND_Gate and_216 is placed but not wired
  // AND_Gate and_217 is placed but not wired
  // AND_Gate and_218 is placed but not wired
  // AND_Gate and_219 is placed but not wired
  // AND_Gate and_220 is placed but not wired
  // AND_Gate and_221 is placed but not wired
  // AND_Gate and_222 is placed but not wired
  // AND_Gate and_223 is placed but not wired
  // AND_Gate and_224 is placed but not wired
  // AND_Gate and_225 is placed but not wired
  // AND_Gate and_226 is placed but not wired
  // AND_Gate and_227 is placed but not wired
  // AND_Gate and_228 is placed but not wired
  // AND_Gate and_229 is placed but not wired
  // AND_Gate and_230 is placed but not wired
  // AND_Gate and_231 is placed but not wired
  // AND_Gate and_232 is placed but not wired
  // AND_Gate and_233 is placed but not wired
  // AND_Gate and_234 is placed but not wired
  // AND_Gate and_235 is placed but not wired
  // AND_Gate and_236 is placed but not wired
  // AND_Gate and_237 is placed but not wired
  // AND_Gate and_238 is placed but not wired
  // AND_Gate and_239 is placed but not wired
  // AND_Gate and_240 is placed but not wired
  // AND_Gate and_241 is placed but not wired
  // AND_Gate and_242 is placed but not wired
  // AND_Gate and_243 is placed but not wired
  // AND_Gate and_244 is placed but not wired
  // AND_Gate and_245 is placed but not wired
  // AND_Gate and_246 is placed but not wired
  // AND_Gate and_247 is placed but not wired
  // AND_Gate and_248 is placed but not wired
  // AND_Gate and_249 is placed but not wired
  // AND_Gate and_250 is placed but not wired
  // AND_Gate and_251 is placed but not wired
  // AND_Gate and_252 is placed but not wired
  // AND_Gate and_253 is placed but not wired
  // AND_Gate and_254 is placed but not wired
  // AND_Gate and_255 is placed but not wired
  // AND_Gate and_256 is placed but not wired
  // AND_Gate and_257 is placed but not wired
  // AND_Gate and_258 is placed but not wired
  // AND_Gate and_259 is placed but not wired
  // AND_Gate and_260 is placed but not wired
  // AND_Gate and_261 is placed but not wired
  // AND_Gate and_262 is placed but not wired
  // AND_Gate and_263 is placed but not wired
  // AND_Gate and_264 is placed but not wired
  // AND_Gate and_265 is placed but not wired
  // AND_Gate and_266 is placed but not wired
  // AND_Gate and_267 is placed but not wired
  // AND_Gate and_268 is placed but not wired
  // AND_Gate and_269 is placed but not wired
  // AND_Gate and_270 is placed but not wired
  // AND_Gate and_271 is placed but not wired
  // AND_Gate and_272 is placed but not wired
  // AND_Gate and_273 is placed but not wired
  // AND_Gate and_274 is placed but not wired
  // AND_Gate and_275 is placed but not wired
  // AND_Gate and_276 is placed but not wired
  // AND_Gate and_277 is placed but not wired
  // AND_Gate and_278 is placed but not wired
  // AND_Gate and_279 is placed but not wired
  // AND_Gate and_280 is placed but not wired
  // AND_Gate and_281 is placed but not wired
  // AND_Gate and_282 is placed but not wired
  // AND_Gate and_283 is placed but not wired
  // AND_Gate and_284 is placed but not wired
  // AND_Gate and_285 is placed but not wired
  // AND_Gate and_286 is placed but not wired
  // AND_Gate and_287 is placed but not wired
  // AND_Gate and_288 is placed but not wired
  // AND_Gate and_289 is placed but not wired
  // AND_Gate and_290 is placed but not wired
  // AND_Gate and_291 is placed but not wired
  // AND_Gate and_292 is placed but not wired
  // AND_Gate and_293 is placed but not wired
  // AND_Gate and_294 is placed but not wired
  // AND_Gate and_295 is placed but not wired
  // AND_Gate and_296 is placed but not wired
  // AND_Gate and_297 is placed but not wired
  // AND_Gate and_298 is placed but not wired
  // AND_Gate and_299 is placed but not wired
  // AND_Gate and_300 is placed but not wired
  // AND_Gate and_301 is placed but not wired
  // AND_Gate and_302 is placed but not wired
  // AND_Gate and_303 is placed but not wired
  // AND_Gate and_304 is placed but not wired
  // AND_Gate and_305 is placed but not wired
  // AND_Gate and_306 is placed but not wired
  // AND_Gate and_307 is placed but not wired
  // AND_Gate and_308 is placed but not wired
  // AND_Gate and_309 is placed but not wired
  // AND_Gate and_310 is placed but not wired
  // AND_Gate and_311 is placed but not wired
  // AND_Gate and_312 is placed but not wired
  // AND_Gate and_313 is placed but not wired
  // AND_Gate and_314 is placed but not wired
  // AND_Gate and_315 is placed but not wired
  // AND_Gate and_316 is placed but not wired
  // AND_Gate and_317 is placed but not wired
  // AND_Gate and_318 is placed but not wired
  // AND_Gate and_319 is placed but not wired
  // AND_Gate and_320 is placed but not wired
  // AND_Gate and_321 is placed but not wired
  // AND_Gate and_322 is placed but not wired
  // AND_Gate and_323 is placed but not wired
  // AND_Gate and_324 is placed but not wired
  // AND_Gate and_325 is placed but not wired
  // AND_Gate and_326 is placed but not wired
  // AND_Gate and_327 is placed but not wired
  // AND_Gate and_328 is placed but not wired
  // AND_Gate and_329 is placed but not wired
  // AND_Gate and_330 is placed but not wired
  // AND_Gate and_331 is placed but not wired
  // AND_Gate and_332 is placed but not wired
  // AND_Gate and_333 is placed but not wired
  // AND_Gate and_334 is placed but not wired
  // AND_Gate and_335 is placed but not wired
  // AND_Gate and_336 is placed but not wired
  // AND_Gate and_337 is placed but not wired
  // AND_Gate and_338 is placed but not wired
  // AND_Gate and_339 is placed but not wired
  // AND_Gate and_340 is placed but not wired
  // AND_Gate and_341 is placed but not wired
  // AND_Gate and_342 is placed but not wired
  // AND_Gate and_343 is placed but not wired
  // AND_Gate and_344 is placed but not wired
  // AND_Gate and_345 is placed but not wired
  // AND_Gate and_346 is placed but not wired
  // AND_Gate and_347 is placed but not wired
  // AND_Gate and_348 is placed but not wired
  // AND_Gate and_349 is placed but not wired
  // AND_Gate and_350 is placed but not wired
  // AND_Gate and_351 is placed but not wired
  // AND_Gate and_352 is placed but not wired
  // AND_Gate and_353 is placed but not wired
  // AND_Gate and_354 is placed but not wired
  // AND_Gate and_355 is placed but not wired
  // AND_Gate and_356 is placed but not wired
  // AND_Gate and_357 is placed but not wired
  // AND_Gate and_358 is placed but not wired
  // AND_Gate and_359 is placed but not wired
  // AND_Gate and_360 is placed but not wired
  // AND_Gate and_361 is placed but not wired
  // AND_Gate and_362 is placed but not wired
  // AND_Gate and_363 is placed but not wired
  // AND_Gate and_364 is placed but not wired
  // AND_Gate and_365 is placed but not wired
  // AND_Gate and_366 is placed but not wired
  // AND_Gate and_367 is placed but not wired
  // AND_Gate and_368 is placed but not wired
  // AND_Gate and_369 is placed but not wired
  // AND_Gate and_370 is placed but not wired
  // AND_Gate and_371 is placed but not wired
  // AND_Gate and_372 is placed but not wired
  // AND_Gate and_373 is placed but not wired
  // AND_Gate and_374 is placed but not wired
  // AND_Gate and_375 is placed but not wired
  // AND_Gate and_376 is placed but not wired
  // AND_Gate and_377 is placed but not wired
  // AND_Gate and_378 is placed but not wired
  // AND_Gate and_379 is placed but not wired
  // AND_Gate and_380 is placed but not wired
  // AND_Gate and_381 is placed but not wired
  // AND_Gate and_382 is placed but not wired
  // AND_Gate and_383 is placed but not wired
  // AND_Gate and_384 is placed but not wired
  // AND_Gate and_385 is placed but not wired
  // AND_Gate and_386 is placed but not wired
  // AND_Gate and_387 is placed but not wired
  // AND_Gate and_388 has open pins: in1=undriven, out=open
  // AND_Gate and_389 is placed but not wired
  // AND_Gate and_390 is placed but not wired
  // AND_Gate and_391 is placed but not wired
  // AND_Gate and_392 is placed but not wired
  // AND_Gate and_393 is placed but not wired
  // AND_Gate and_394 is placed but not wired
  // AND_Gate and_395 is placed but not wired
  // AND_Gate and_396 is placed but not wired
  // AND_Gate and_397 is placed but not wired
  // AND_Gate and_398 is placed but not wired
  // AND_Gate and_399 is placed but not wired
  // AND_Gate and_400 is placed but not wired
  // AND_Gate and_401 is placed but not wired
  // AND_Gate and_402 is placed but not wired
  // AND_Gate and_403 is placed but not wired
  // AND_Gate and_404 is placed but not wired
  // AND_Gate and_405 is placed but not wired
  // AND_Gate and_406 is placed but not wired
  // AND_Gate and_407 is placed but not wired
  // AND_Gate and_408 is placed but not wired
  // AND_Gate and_409 is placed but not wired
  // AND_Gate and_410 is placed but not wired
  // AND_Gate and_411 is placed but not wired
  // AND_Gate and_412 is placed but not wired
  // AND_Gate and_413 is placed but not wired
  // AND_Gate and_414 is placed but not wired
  // AND_Gate and_415 is placed but not wired
  // AND_Gate and_416 is placed but not wired
  // AND_Gate and_417 is placed but not wired
  // AND_Gate and_418 is placed but not wired
  // AND_Gate and_419 is placed but not wired
  // AND_Gate and_420 is placed but not wired
  // AND_Gate and_421 is placed but not wired
  // AND_Gate and_422 is placed but not wired
  // AND_Gate and_423 is placed but not wired
  // AND_Gate and_424 is placed but not wired
  // AND_Gate and_425 is placed but not wired
  // AND_Gate and_426 is placed but not wired
  // AND_Gate and_427 is placed but not wired
  // AND_Gate and_428 is placed but not wired
  // AND_Gate and_429 is placed but not wired
  // AND_Gate and_430 is placed but not wired
  // AND_Gate and_431 is placed but not wired
  // AND_Gate and_432 is placed but not wired
  // AND_Gate and_433 is placed but not wired
  // AND_Gate and_434 is placed but not wired
  // AND_Gate and_435 is placed but not wired
  // AND_Gate and_436 is placed but not wired
  // AND_Gate and_437 is placed but not wired
  // AND_Gate and_438 is placed but not wired
  // AND_Gate and_439 is placed but not wired
  // AND_Gate and_440 is placed but not wired
  // AND_Gate and_441 is placed but not wired
  // AND_Gate and_442 is placed but not wired
  // AND_Gate and_443 is placed but not wired
  // AND_Gate and_444 is placed but not wired
  // AND_Gate and_445 is placed but not wired
  // AND_Gate and_446 is placed but not wired
  // AND_Gate and_447 is placed but not wired
  // AND_Gate and_448 is placed but not wired
  // AND_Gate and_449 is placed but not wired
  // AND_Gate and_450 is placed but not wired
  // AND_Gate and_451 is placed but not wired
  // AND_Gate and_452 is placed but not wired
  // AND_Gate and_453 is placed but not wired
  // AND_Gate and_454 is placed but not wired
  // AND_Gate and_455 is placed but not wired
  // AND_Gate and_456 is placed but not wired
  // AND_Gate and_457 is placed but not wired
  // AND_Gate and_458 is placed but not wired
  // AND_Gate and_459 is placed but not wired
  // AND_Gate and_460 is placed but not wired
  // AND_Gate and_461 is placed but not wired
  // AND_Gate and_462 is placed but not wired
  // AND_Gate and_463 is placed but not wired
  // AND_Gate and_464 is placed but not wired
  // AND_Gate and_465 is placed but not wired
  // AND_Gate and_466 is placed but not wired
  // AND_Gate and_467 is placed but not wired
  // AND_Gate and_468 is placed but not wired
  // AND_Gate and_469 is placed but not wired
  // AND_Gate and_470 is placed but not wired
  // AND_Gate and_471 is placed but not wired
  // AND_Gate and_472 is placed but not wired
  // AND_Gate and_473 is placed but not wired
  // AND_Gate and_474 is placed but not wired
  // AND_Gate and_475 is placed but not wired
  // AND_Gate and_476 is placed but not wired
  // AND_Gate and_477 is placed but not wired
  // AND_Gate and_478 is placed but not wired
  // AND_Gate and_479 is placed but not wired
  // AND_Gate and_480 is placed but not wired
  // AND_Gate and_481 is placed but not wired
  // AND_Gate and_482 is placed but not wired
  // AND_Gate and_483 is placed but not wired
  // AND_Gate and_484 is placed but not wired
  // AND_Gate and_485 is placed but not wired
  // AND_Gate and_486 is placed but not wired
  // AND_Gate and_487 is placed but not wired
  // AND_Gate and_488 is placed but not wired
  // AND_Gate and_489 is placed but not wired
  // AND_Gate and_490 is placed but not wired
  // AND_Gate and_491 is placed but not wired
  // AND_Gate and_492 is placed but not wired
  // AND_Gate and_493 is placed but not wired
  // AND_Gate and_494 is placed but not wired
  // AND_Gate and_495 is placed but not wired
  // AND_Gate and_496 is placed but not wired
  // AND_Gate and_497 is placed but not wired
  // AND_Gate and_498 is placed but not wired
  // AND_Gate and_499 is placed but not wired
  // AND_Gate and_500 is placed but not wired
  // AND_Gate and_501 is placed but not wired
  // AND_Gate and_502 is placed but not wired
  // AND_Gate and_503 is placed but not wired
  // AND_Gate and_504 is placed but not wired
  // AND_Gate and_505 is placed but not wired
  // AND_Gate and_506 is placed but not wired
  // AND_Gate and_507 is placed but not wired
  // AND_Gate and_508 is placed but not wired
  // AND_Gate and_509 is placed but not wired
  // AND_Gate and_510 is placed but not wired
  // AND_Gate and_511 is placed but not wired
  // AND_Gate and_512 is placed but not wired
  // AND_Gate and_513 is placed but not wired
  // AND_Gate and_514 is placed but not wired
  // AND_Gate and_515 is placed but not wired
  // AND_Gate and_516 is placed but not wired
  // AND_Gate and_517 is placed but not wired
  // AND_Gate and_518 is placed but not wired
  // AND_Gate and_519 is placed but not wired
  // AND_Gate and_520 is placed but not wired
  // AND_Gate and_521 is placed but not wired
  // AND_Gate and_522 is placed but not wired
  // AND_Gate and_523 is placed but not wired
  // AND_Gate and_524 is placed but not wired
  // AND_Gate and_525 is placed but not wired
  // AND_Gate and_526 is placed but not wired
  // AND_Gate and_527 is placed but not wired
  // AND_Gate and_528 is placed but not wired
  // AND_Gate and_529 is placed but not wired
  // AND_Gate and_530 is placed but not wired
  // AND_Gate and_531 is placed but not wired
  // AND_Gate and_532 is placed but not wired
  // AND_Gate and_533 is placed but not wired
  // AND_Gate and_534 is placed but not wired
  // AND_Gate and_535 is placed but not wired
  // AND_Gate and_536 is placed but not wired
  mem_dados mem_dados_1 (.EL(and_1_out), .WD(in_1));  // open: LD, memWrite, memRead_2, memRead
  mem_dados mem_dados_2 (.EL(and_2_out), .WD(in_1));  // open: LD, memWrite, memRead_2, memRead
  mem_dados mem_dados_3 (.EL(and_3_out), .WD(in_1));  // open: LD, memWrite, memRead_2, memRead
  mem_dados mem_dados_4 (.EL(and_4_out), .WD(in_1));  // open: LD, memWrite, memRead_2, memRead
  mem_dados mem_dados_5 (.EL(and_5_out), .WD(in_1));  // open: LD, memWrite, memRead_2, memRead
  mem_dados mem_dados_6 (.EL(and_6_out), .WD(in_1));  // open: LD, memWrite, memRead_2, memRead
  mem_dados mem_dados_7 (.EL(and_7_out), .WD(in_1));  // open: LD, memWrite, memRead_2, memRead
  mem_dados mem_dados_8 (.EL(and_8_out), .WD(in_1));  // open: LD, memWrite, memRead_2, memRead
  mem_dados mem_dados_9 (.EL(and_9_out), .WD(in_1));  // open: LD, memWrite, memRead_2, memRead
  mem_dados mem_dados_10 (.EL(and_10_out), .WD(in_1));  // open: LD, memWrite, memRead_2, memRead
  mem_dados mem_dados_11 (.EL(and_11_out), .WD(in_1));  // open: LD, memWrite, memRead_2, memRead
  mem_dados mem_dados_12 (.EL(and_12_out), .WD(in_1));  // open: LD, memWrite, memRead_2, memRead
  mem_dados mem_dados_13 (.EL(and_13_out), .WD(in_1));  // open: LD, memWrite, memRead_2, memRead
  mem_dados mem_dados_14 (.EL(and_14_out), .WD(in_1));  // open: LD, memWrite, memRead_2, memRead
  mem_dados mem_dados_15 (.EL(and_15_out), .WD(in_1));  // open: LD, memWrite, memRead_2, memRead
  mem_dados mem_dados_16 (.EL(and_16_out), .WD(in_1));  // open: LD, memWrite, memRead_2, memRead
  mem_dados mem_dados_17 (.EL(and_17_out), .WD(in_1));  // open: LD, memWrite, memRead_2, memRead
  mem_dados mem_dados_18 (.EL(and_18_out), .WD(in_1));  // open: LD, memWrite, memRead_2, memRead
  mem_dados mem_dados_19 (.EL(and_19_out), .WD(in_1));  // open: LD, memWrite, memRead_2, memRead
  mem_dados mem_dados_20 (.EL(and_20_out), .WD(in_1));  // open: LD, memWrite, memRead_2, memRead
  mem_dados mem_dados_21 (.EL(and_21_out), .WD(in_1));  // open: LD, memWrite, memRead_2, memRead
  mem_dados mem_dados_22 (.EL(and_22_out), .WD(in_1));  // open: LD, memWrite, memRead_2, memRead
  mem_dados mem_dados_23 (.EL(and_23_out), .WD(in_1));  // open: LD, memWrite, memRead_2, memRead
  mem_dados mem_dados_24 (.EL(and_24_out), .WD(in_1));  // open: LD, memWrite, memRead_2, memRead
  mem_dados mem_dados_25 (.EL(and_25_out), .WD(in_1));  // open: LD, memWrite, memRead_2, memRead
  mem_dados mem_dados_26 (.EL(and_26_out), .WD(in_1));  // open: LD, memWrite, memRead_2, memRead
  mem_dados mem_dados_27 (.EL(and_27_out), .WD(in_1));  // open: LD, memWrite, memRead_2, memRead
  mem_dados mem_dados_28 (.EL(and_28_out), .WD(in_1));  // open: LD, memWrite, memRead_2, memRead
  mem_dados mem_dados_29 (.EL(and_29_out), .WD(in_1));  // open: LD, memWrite, memRead_2, memRead
  mem_dados mem_dados_30 (.EL(and_30_out), .WD(in_1));  // open: LD, memWrite, memRead_2, memRead
  mem_dados mem_dados_31 (.EL(and_31_out), .WD(in_1));  // open: LD, memWrite, memRead_2, memRead
  mem_dados mem_dados_32 (.EL(and_32_out), .WD(in_1));  // open: LD, memWrite, memRead_2, memRead
  mem_dados mem_dados_33 (.EL(and_33_out), .WD(in_1));  // open: LD, memWrite, memRead_2, memRead
  mem_dados mem_dados_34 (.EL(and_34_out), .WD(in_1));  // open: LD, memWrite, memRead_2, memRead
  mem_dados mem_dados_35 (.EL(and_35_out), .WD(in_1));  // open: LD, memWrite, memRead_2, memRead
  mem_dados mem_dados_36 (.EL(and_36_out), .WD(in_1));  // open: LD, memWrite, memRead_2, memRead
  mem_dados mem_dados_37 (.EL(and_37_out), .WD(in_1));  // open: LD, memWrite, memRead_2, memRead
  mem_dados mem_dados_38 (.EL(and_38_out), .WD(in_1));  // open: LD, memWrite, memRead_2, memRead
  mem_dados mem_dados_39 (.EL(and_39_out), .WD(in_1));  // open: LD, memWrite, memRead_2, memRead
  mem_dados mem_dados_40 (.EL(and_40_out), .WD(in_1));  // open: LD, memWrite, memRead_2, memRead
  mem_dados mem_dados_41 (.EL(and_41_out), .WD(in_1));  // open: LD, memWrite, memRead_2, memRead
  mem_dados mem_dados_42 (.EL(and_42_out), .WD(in_1));  // open: LD, memWrite, memRead_2, memRead
  mem_dados mem_dados_43 (.EL(and_43_out), .WD(in_1));  // open: LD, memWrite, memRead_2, memRead
  mem_dados mem_dados_44 (.EL(and_44_out), .WD(in_1));  // open: LD, memWrite, memRead_2, memRead
  mem_dados mem_dados_45 (.EL(undriven_2), .WD(in_1));  // open: LD, memWrite, memRead_2, memRead
  mem_dados mem_dados_46 (.EL(undriven_3), .WD(in_1));  // open: LD, memWrite, memRead_2, memRead
  mem_dados mem_dados_47 (.EL(and_47_out), .WD(in_1));  // open: LD, memWrite, memRead_2, memRead
  mem_dados mem_dados_48 (.EL(undriven_4), .WD(in_1));  // open: LD, memWrite, memRead_2, memRead
  mem_dados mem_dados_49 (.EL(undriven_5), .WD(in_1));  // open: LD, memWrite, memRead_2, memRead
  mem_dados mem_dados_50 (.EL(and_50_out), .WD(in_1));  // open: LD, memWrite, memRead_2, memRead
  mem_dados mem_dados_51 (.EL(and_51_out), .WD(in_1));  // open: LD, memWrite, memRead_2, memRead
  mem_dados mem_dados_52 (.EL(and_52_out), .WD(in_1));  // open: LD, memWrite, memRead_2, memRead
  mem_dados mem_dados_53 (.EL(and_53_out), .WD(in_1));  // open: LD, memWrite, memRead_2, memRead
  mem_dados mem_dados_54 (.EL(and_54_out), .WD(in_1));  // open: LD, memWrite, memRead_2, memRead
endmodule
