// Logisim project controle.circ as structural Verilog
module controle (
  input  [5:0] in_1,
  output out_2
);

  and and_1 (out_2, ~in_1[0], ~in_1[1], ~in_1[2], ~in_1[3], ~in_1[4], ~in_1[5]);  // AND_Gate
  // AND_Gate and_2 is placed but not wired
endmodule
